// Logisim project Computer8Bit.circ as structural Verilog: 18 circuits, main circuit main
module main (
);

  wire button_1_out, C1, C2, C3, C4, CSPC_DIR, FLAGS_MODE_SEL0, FLAGS_MODE_SEL1,
       flagscontroller_1_flags_in_sel, flagscontroller_1_not_czn_in, flagscontroller_1_not_i_in, I_VAL, J,
       JA, JC, JN, JZ, keyboard_1_avail, keyboardadapter_1_k_clear, keyboardadapter_1_k_clk,
       keyboardadapter_1_k_read_en, not_1_out, not_2_out, not_3_out, not_4_out, not_5_out, not_6_out,
       not_7_out, not_8_out, not_9_out, NOT_ABH_IN, NOT_ABL_IN, NOT_CS_IN, NOT_CS_OUT, NOT_DATA_LATCH_OUT,
       NOT_DEVICE_IN, NOT_DEVICE_OUT, NOT_DEVICE_SEL_0, NOT_DEVICE_SEL_1, NOT_DEVICE_SEL_2, NOT_DEVICE_SEL_3,
       NOT_DEVICE_SEL_4, NOT_DEVICE_SEL_5, NOT_DEVICE_SEL_RAM, NOT_DEVICE_SEL_ROM, NOT_FETCH, NOT_FLAGS_OUT,
       NOT_HLT, NOT_IRQ, NOT_IVH_OUT, NOT_IVL_OUT, NOT_PASS, NOT_PC_IN, NOT_PC_INC, NOT_PC_OUT, NOT_POP,
       NOT_PUSH, NOT_RA_IN, NOT_RA_OUT, NOT_RA_SL, NOT_RA_SR, NOT_RB_IN, NOT_RB_OUT, NOT_RC_IN, NOT_RC_OUT,
       NOT_RD_IN, NOT_RD_OUT, NOT_RT_IN, NOT_RT_OUT, NOT_SP_CT, NOT_SP_IN, NOT_SS_IN, OP_SEL0, OP_SEL1,
       OP_SEL2, or_1_out, or_2_out, or_3_out, or_4_out, or_5_out, or_6_out, or_7_out, or_8_out, or_9_out,
       PAGE_0, RESET, ROM_AS, SP_DIR, switch_1_p2, X_SEL0, X_SEL1, Y_SEL0, Y_SEL1, Y_SEL2;
  wire [2:0] alu_1_flags;
  wire [3:0] flagsregister_1_flags_out, hexdisplayadapter_1_lsb, hexdisplayadapter_1_msb, undriven_2,
       undriven_3;
  wire [6:0] keyboard_1_data;
  wire [7:0] ABH_q, aluoperandselector_1_o1, aluoperandselector_1_o2, aluoperatorselector_1_op_out,
       bufferedregister_1_async_out, DATA_LATCH_q, DBUS, RA_async_out, RB_async_out, RC_async_out,
       RD_async_out, rommodule_1_ir_out, SP_sp_out, SS_q, undriven;
  wire [12:0] codesegment_programcounter_1_cs_pc;
  wire [15:0] ABUS;

  // DipSwitch dipswitch_1: pin names not known
  assign DBUS = switch_1_p2 ? undriven : 8'bz;  // Controlled_Buffer controlled_buffer_1
  // Switch switch_1: pin names not known; wires that end beside it: 1'b1, switch_1_p2
  Pull_Resistor pull_resistor_1 (.node(switch_1_p2));
  Hex_Digit_Display hex_digit_display_1 (.value(DBUS[7:4]));  // open: dp
  Hex_Digit_Display hex_digit_display_2 (.value(DBUS[3:0]));  // open: dp
  LED led_1 (.in(NOT_RA_IN));
  ControlUnit controlunit_1 (
    .DATA_LATCH(DATA_LATCH_q), .NOT_IRQ(NOT_IRQ), .CLK90(C1), .RESET(RESET),
    .I(flagsregister_1_flags_out[3]), .NOT_RA_IN(NOT_RA_IN), .NOT_RA_OUT(NOT_RA_OUT), .NOT_RA_SL(NOT_RA_SL),
    .NOT_RA_SR(NOT_RA_SR), .NOT_RB_IN(NOT_RB_IN), .NOT_RB_OUT(NOT_RB_OUT), .NOT_RC_IN(NOT_RC_IN),
    .NOT_RC_OUT(NOT_RC_OUT), .NOT_RD_IN(NOT_RD_IN), .NOT_RD_OUT(NOT_RD_OUT), .NOT_DEVICE_IN(NOT_DEVICE_IN),
    .NOT_DEVICE_OUT(NOT_DEVICE_OUT), .NOT_SS_IN(NOT_SS_IN), .NOT_SP_IN(NOT_SP_IN), .NOT_SP_CT(NOT_SP_CT),
    .SP_DIR(SP_DIR), .NOT_ABH_IN(NOT_ABH_IN), .NOT_ABL_IN(NOT_ABL_IN), .NOT_RT_IN(NOT_RT_IN),
    .NOT_RT_OUT(NOT_RT_OUT), .X_SEL0(X_SEL0), .X_SEL1(X_SEL1), .Y_SEL0(Y_SEL0), .Y_SEL1(Y_SEL1),
    .Y_SEL2(Y_SEL2), .OP_SEL0(OP_SEL0), .OP_SEL1(OP_SEL1), .OP_SEL2(OP_SEL2), .ROM_AS(ROM_AS),
    .NOT_CS_IN(NOT_CS_IN), .NOT_PC_IN(NOT_PC_IN), .NOT_PC_INC(NOT_PC_INC), .NOT_CS_OUT(NOT_CS_OUT),
    .NOT_PC_OUT(NOT_PC_OUT), .NOT_FETCH(NOT_FETCH), .J(J), .JC(JC), .JZ(JZ), .JN(JN), .JA(JA),
    .NOT_PASS(NOT_PASS), .NOT_HLT(NOT_HLT), .PAGE_0(PAGE_0), .NOT_PUSH(NOT_PUSH), .NOT_POP(NOT_POP),
    .NOT_DATA_LATCH_OUT(NOT_DATA_LATCH_OUT), .NOT_IVH_OUT(NOT_IVH_OUT), .NOT_IVL_OUT(NOT_IVL_OUT),
    .I_VAL(I_VAL), .FLAGS_MODE_SEL0(FLAGS_MODE_SEL0), .FLAGS_MODE_SEL1(FLAGS_MODE_SEL1),
    .NOT_FLAGS_OUT(NOT_FLAGS_OUT), .CSPC_DIR(CSPC_DIR));
  LED led_2 (.in(NOT_RA_OUT));
  LED led_3 (.in(NOT_RA_SL));
  LED led_4 (.in(NOT_RA_SR));
  LED led_5 (.in(NOT_RB_IN));
  LED led_6 (.in(NOT_RB_OUT));
  LED led_7 (.in(NOT_RC_IN));
  LED led_8 (.in(NOT_RC_OUT));
  LED led_9 (.in(NOT_RD_IN));
  LED led_10 (.in(NOT_RD_OUT));
  LED led_11 (.in(NOT_DEVICE_IN));
  LED led_12 (.in(NOT_DEVICE_OUT));
  LED led_13 (.in(NOT_SS_IN));
  LED led_14 (.in(NOT_SP_IN));
  LED led_15 (.in(NOT_SP_CT));
  LED led_16 (.in(SP_DIR));
  LED led_17 (.in(NOT_ABH_IN));
  LED led_18 (.in(NOT_ABL_IN));
  LED led_19 (.in(NOT_RT_IN));
  LED led_20 (.in(NOT_RT_OUT));
  LED led_21 (.in(X_SEL0));
  LED led_22 (.in(X_SEL1));
  LED led_23 (.in(Y_SEL0));
  LED led_24 (.in(Y_SEL1));
  LED led_25 (.in(Y_SEL2));
  LED led_26 (.in(OP_SEL0));
  LED led_27 (.in(OP_SEL1));
  LED led_28 (.in(OP_SEL2));
  LED led_29 (.in(ROM_AS));
  LED led_30 (.in(NOT_CS_IN));
  LED led_31 (.in(NOT_PC_IN));
  LED led_32 (.in(NOT_PC_INC));
  LED led_33 (.in(NOT_CS_OUT));
  LED led_34 (.in(NOT_PC_OUT));
  LED led_35 (.in(NOT_FETCH));
  LED led_36 (.in(J));
  LED led_37 (.in(JC));
  LED led_38 (.in(JZ));
  LED led_39 (.in(JN));
  LED led_40 (.in(JA));
  LED led_41 (.in(NOT_PASS));
  LED led_42 (.in(NOT_HLT));
  LED led_43 (.in(PAGE_0));
  LED led_44 (.in(NOT_PUSH));
  LED led_45 (.in(NOT_POP));
  LED led_46 (.in(NOT_DATA_LATCH_OUT));
  LED led_47 (.in(NOT_IVH_OUT));
  LED led_48 (.in(NOT_IVL_OUT));
  LED led_49 (.in(I_VAL));
  LED led_50 (.in(FLAGS_MODE_SEL0));
  LED led_51 (.in(FLAGS_MODE_SEL1));
  LED led_52 (.in(NOT_FLAGS_OUT));
  LED led_53 (.in(CSPC_DIR));
  Pull_Resistor #(.pull(1)) pull_resistor_2 (.node(NOT_IRQ));
  or or_1 (or_1_out, NOT_DEVICE_SEL_0, NOT_DEVICE_IN);
  or or_2 (or_2_out, NOT_DEVICE_SEL_0, NOT_DEVICE_OUT);
  or or_3 (or_3_out, NOT_DEVICE_SEL_3, NOT_DEVICE_IN);
  not not_1 (not_1_out, or_3_out);
  Keyboard keyboard_1 (
    .clk(keyboardadapter_1_k_clk), .re(keyboardadapter_1_k_read_en), .clr(keyboardadapter_1_k_clear),
    .avail(keyboard_1_avail), .data(keyboard_1_data));
  Hex_Digit_Display hex_digit_display_3 (.value(ABUS[15:12]));  // open: dp
  Hex_Digit_Display hex_digit_display_4 (.value(ABUS[11:8]));  // open: dp
  // RGB_Video #(.height(64), .width(64)) rgb_video_1: pin names not known; wires that end beside it: NOT_DEVICE_SEL_4, NOT_DEVICE_SEL_5, C4, not_1_out, ABUS[5:0], ABUS[11:6], DBUS
  Hex_Digit_Display hex_digit_display_5 (.value(ABUS[7:4]));  // open: dp
  Hex_Digit_Display hex_digit_display_6 (.value(ABUS[3:0]));  // open: dp
  KeyboardAdapter keyboardadapter_1 (
    .K_AVAIL(keyboard_1_avail), .K_DATA(keyboard_1_data), .BUS_IN(DBUS), .ABUS(ABUS),
    .NOT_DEVICE_IN(or_1_out), .NOT_DEVICE_OUT(or_2_out), .CLK(C4), .NOT_IRQ(NOT_IRQ), .BUS_OUT(DBUS),
    .K_READ_EN(keyboardadapter_1_k_read_en), .K_CLEAR(keyboardadapter_1_k_clear),
    .K_CLK(keyboardadapter_1_k_clk));
  Pull_Resistor pull_resistor_3 (.node(RESET));
  // Switch RESET: pin names not known; wires that end beside it: 1'b1, RESET
  Register ABH (.D(DBUS), .en(not_2_out), .clk(C4), .Q(ABH_q));  // open: clr
  not not_2 (not_2_out, NOT_ABH_IN);
  or or_4 (or_4_out, NOT_DEVICE_SEL_1, NOT_DEVICE_IN);
  or or_5 (or_5_out, NOT_DEVICE_SEL_1, NOT_DEVICE_OUT);
  Keyboard keyboard_2 ();  // open: clk, re, clr, avail, data
  Register SS (.D(DBUS), .en(not_3_out), .clk(C4), .Q(SS_q), .clr(1'b0));
  not not_3 (not_3_out, NOT_SS_IN);
  Register ABL (.D(DBUS), .en(not_4_out), .clk(C4), .Q(ABUS[7:0]));  // open: clr
  not not_4 (not_4_out, NOT_ABL_IN);
  Multiplexer #(.width(8)) multiplexer_1 (.in0(ABH_q), .in1({8{1'b0}}), .out(ABUS[15:8]), .sel(PAGE_0));
  AddrDecoder addrdecoder_1 (
    .ABUS(ABUS), .NOT_DEVICE_SEL_RAM(NOT_DEVICE_SEL_RAM), .NOT_DEVICE_SEL_ROM(NOT_DEVICE_SEL_ROM),
    .NOT_DEVICE_SEL_0(NOT_DEVICE_SEL_0), .NOT_DEVICE_SEL_1(NOT_DEVICE_SEL_1),
    .NOT_DEVICE_SEL_2(NOT_DEVICE_SEL_2), .NOT_DEVICE_SEL_3(NOT_DEVICE_SEL_3),
    .NOT_DEVICE_SEL_4(NOT_DEVICE_SEL_4), .NOT_DEVICE_SEL_5(NOT_DEVICE_SEL_5));
  StackPointer SP (.NOT_SP_IN(NOT_SP_IN), .SP_DIR(SP_DIR), .NOT_SP_CT(NOT_SP_CT), .CLK(C3), .SP_OUT(SP_sp_out));
  CodeSegment_ProgramCounter codesegment_programcounter_1 (
    .FLAGS(flagsregister_1_flags_out), .J(J), .JC(JC), .JZ(JZ), .JN(JN), .JA(JA), .NOT_PC_IN(NOT_PC_IN),
    .NOT_CS_IN(NOT_CS_IN), .NOT_PC_INC(NOT_PC_INC), .RESET(RESET), .ABUS(ABUS), .CLK(C3),
    .NOT_PC_OUT(NOT_PC_OUT), .NOT_CS_OUT(NOT_CS_OUT), .CSPC_DIR(CSPC_DIR),
    .CS_PC(codesegment_programcounter_1_cs_pc), .BUS_OUT(DBUS));
  Hex_Digit_Display hex_digit_display_7 (.value(hexdisplayadapter_1_msb));  // open: dp
  HexDisplayAdapter hexdisplayadapter_1 (
    .DBUS_IN(DBUS), .ABUS(ABUS), .NOT_DEVICE_IN(or_4_out), .NOT_DEVICE_OUT(or_5_out), .CLK(C4),
    .LSB(hexdisplayadapter_1_lsb), .MSB(hexdisplayadapter_1_msb));
  Hex_Digit_Display hex_digit_display_8 (.value(hexdisplayadapter_1_lsb));  // open: dp
  Register DATA_LATCH (.D(rommodule_1_ir_out), .en(not_5_out), .clk(C2), .Q(DATA_LATCH_q), .clr(RESET));
  not not_5 (not_5_out, NOT_FETCH);
  not not_6 (not_6_out, NOT_DATA_LATCH_OUT);
  assign DBUS = not_6_out ? DATA_LATCH_q : 8'bz;  // Controlled_Buffer controlled_buffer_2
  BufferedRegister bufferedregister_1 (
    .BUS_IN(DBUS), .CLK(C4), .NOT_R_IN(NOT_RT_IN), .NOT_R_OUT(NOT_RT_OUT),
    .ASYNC_OUT(bufferedregister_1_async_out), .BUS_OUT(DBUS));
  or or_6 (or_6_out, NOT_DEVICE_SEL_2, NOT_DEVICE_IN);
  or or_7 (or_7_out, NOT_DEVICE_SEL_2, NOT_DEVICE_OUT);
  ClockModule clockmodule_1 (.NOT_HLT(NOT_HLT), .C2(C2), .C1(C1), .C4(C4), .C3(C3));
  RAMModule rammodule_1 (
    .NOT_PUSH(NOT_PUSH), .NOT_DEVICE_IN(NOT_DEVICE_IN), .BUS_IN(DBUS),
    .NOT_DEVICE_SEL_RAM(NOT_DEVICE_SEL_RAM), .SP(SP_sp_out), .NOT_DEVICE_OUT(NOT_DEVICE_OUT),
    .NOT_POP(NOT_POP), .CLK(C4), .SS(SS_q), .ABUS(ABUS), .BUS_OUT(DBUS));
  ROMModule rommodule_1 (
    .ABUS(ABUS), .CS_PC(codesegment_programcounter_1_cs_pc), .ROM_AS(ROM_AS), .CLK(C3),
    .NOT_DEVICE_SEL_ROM(NOT_DEVICE_SEL_ROM), .NOT_DEVICE_OUT(NOT_DEVICE_OUT), .NOT_FETCH(NOT_FETCH),
    .BUS_OUT(DBUS), .IR_OUT(rommodule_1_ir_out));
  Button button_1 (.out(button_1_out));
  not not_7 (not_7_out, NOT_IVL_OUT);
  assign DBUS = not_7_out ? {8{1'b0}} : 8'bz;  // Controlled_Buffer controlled_buffer_3
  assign DBUS = not_8_out ? 8'h1f : 8'bz;  // Controlled_Buffer controlled_buffer_4
  not not_8 (not_8_out, NOT_IVH_OUT);
  BufferedRegister RC (
    .BUS_IN(DBUS), .CLK(C4), .NOT_R_IN(NOT_RC_IN), .NOT_R_OUT(NOT_RC_OUT), .ASYNC_OUT(RC_async_out),
    .BUS_OUT(DBUS));
  Hex_Digit_Display hex_digit_display_9 (.value(RC_async_out[7:4]));  // open: dp
  ShiftRegister RA (
    .NOT_SR(NOT_RA_SR), .NOT_IE(NOT_RA_IN), .NOT_SL(NOT_RA_SL), .CLK(C4), .BUS_IN(DBUS), .NOT_OE(NOT_RA_OUT),
    .ASYNC_OUT(RA_async_out), .BUS_OUT(DBUS));
  Hex_Digit_Display hex_digit_display_10 (.value(RA_async_out[7:4]));  // open: dp
  Hex_Digit_Display hex_digit_display_11 (.value(RC_async_out[3:0]));  // open: dp
  Hex_Digit_Display hex_digit_display_12 (.value(RA_async_out[3:0]));  // open: dp
  ALUOperandSelector aluoperandselector_1 (
    .X_SEL0(X_SEL0), .X_SEL1(X_SEL1), .Y_SEL0(Y_SEL0), .Y_SEL1(Y_SEL1), .Y_SEL2(Y_SEL2),
    .A_ASYNC(RA_async_out), .B_ASYNC(RB_async_out), .C_ASYNC(RC_async_out), .D_ASYNC(RD_async_out),
    .E_ASYNC(bufferedregister_1_async_out), .F_ASYNC(8'h1), .O1(aluoperandselector_1_o1),
    .O2(aluoperandselector_1_o2));
  or or_8 (or_8_out, NOT_DEVICE_SEL_3, NOT_DEVICE_IN);
  or or_9 (or_9_out, NOT_DEVICE_SEL_3, NOT_DEVICE_OUT);
  FLAGSController flagscontroller_1 (
    .FLAGS_MODE_SEL0(FLAGS_MODE_SEL0), .FLAGS_MODE_SEL1(FLAGS_MODE_SEL1),
    .NOT_CZN_IN(flagscontroller_1_not_czn_in), .NOT_I_IN(flagscontroller_1_not_i_in),
    .FLAGS_IN_SEL(flagscontroller_1_flags_in_sel));
  BufferedRegister RB (
    .BUS_IN(DBUS), .CLK(C4), .NOT_R_IN(NOT_RB_IN), .NOT_R_OUT(NOT_RB_OUT), .ASYNC_OUT(RB_async_out),
    .BUS_OUT(DBUS));
  BufferedRegister RD (
    .BUS_IN(DBUS), .CLK(C4), .NOT_R_IN(NOT_RD_IN), .NOT_R_OUT(NOT_RD_OUT), .ASYNC_OUT(RD_async_out),
    .BUS_OUT(DBUS));
  Hex_Digit_Display hex_digit_display_13 (.value(RD_async_out[7:4]));  // open: dp
  Hex_Digit_Display hex_digit_display_14 (.value(RD_async_out[3:0]));  // open: dp
  Hex_Digit_Display hex_digit_display_15 (.value(RB_async_out[7:4]));  // open: dp
  Hex_Digit_Display hex_digit_display_16 (.value(RB_async_out[3:0]));  // open: dp
  ALUOperatorSelector aluoperatorselector_1 (
    .OP_SEL0(OP_SEL0), .OP_SEL1(OP_SEL1), .OP_SEL2(OP_SEL2), .OP_OUT(aluoperatorselector_1_op_out));
  ALU alu_1 (
    .OPERATORS(aluoperatorselector_1_op_out), .O1(aluoperandselector_1_o1), .O2(aluoperandselector_1_o2),
    .BUS_OUT(DBUS), .FLAGS(alu_1_flags));
  FLAGSRegister flagsregister_1 (
    .BUS_IN(DBUS), .I_VAL(I_VAL), .ALU_FLAGS(alu_1_flags), .NOT_CZN_IN(flagscontroller_1_not_czn_in),
    .NOT_I_IN(flagscontroller_1_not_i_in), .FLAGS_IN_SEL(flagscontroller_1_flags_in_sel), .CLK(C4),
    .FLAGS_OUT(flagsregister_1_flags_out));
  LED led_54 (.in(flagsregister_1_flags_out[3]));
  LED led_55 (.in(flagsregister_1_flags_out[2]));
  LED led_56 (.in(flagsregister_1_flags_out[1]));
  Hex_Digit_Display hex_digit_display_17 (.value(undriven_2));  // open: dp
  LED led_57 (.in(flagsregister_1_flags_out[0]));
  not not_9 (not_9_out, NOT_FLAGS_OUT);
  assign DBUS = not_9_out ? {4'b0000, flagsregister_1_flags_out} : 8'bz;  // Controlled_Buffer controlled_buffer_5
  Hex_Digit_Display hex_digit_display_18 (.value(undriven_3));  // open: dp

  // Notes on the sheet:
  //   Write to bus
  //   Data bus
  //   Address bus
  //   1. control 2. fetch 3. PC increment 4. data
  //   ROM
  //   Clock
  //   RAM
  //   DATA_LATCH
  //   RT
  //   RC
  //   RA
  //   ALU_OPERAND_SELECTOR
  //   RD
  //   RB
  //   ALU_OPERATOR_SELECTOR
  //   I
  //   N
  //   Z
  //   C
endmodule

module ShiftRegister (
  input  NOT_SR,
  input  NOT_IE,
  input  NOT_SL,
  input  CLK,
  input  [7:0] BUS_IN,
  input  NOT_OE,
  output [7:0] ASYNC_OUT,
  output [7:0] BUS_OUT
);

  wire not_1_out, S0_out, S1_out;

  not not_1 (not_1_out, NOT_OE);
  nand S0 (S0_out, NOT_SR, NOT_IE);
  nand S1 (S1_out, NOT_IE, NOT_SL);
  L_8_bit_universal_shift_storage_register_with_3_state_outputs_SN74ALS299_87cfe9f2 l_8_bit_universal_shift_storage_register_with_3_state_outputs_sn74als299_87cfe9f2_1 (
    .CLK(CLK), .NOT_CLR(1'b1), .NOT_OE1(1'b0), .NOT_OE2(1'b0), .BUS_IN(BUS_IN), .S1(S1_out), .SR(1'b0),
    .S0(S0_out), .SL(1'b0), .BUS_OUT(ASYNC_OUT));  // open: QA1, QH1
  assign BUS_OUT = not_1_out ? ASYNC_OUT : 8'bz;  // Controlled_Buffer controlled_buffer_1
endmodule

module BufferedRegister (
  input  [7:0] BUS_IN,
  input  CLK,
  input  NOT_R_IN,
  input  NOT_R_OUT,
  output [7:0] ASYNC_OUT,
  output [7:0] BUS_OUT
);

  wire not_1_out, not_2_out;

  not not_1 (not_1_out, NOT_R_IN);
  not not_2 (not_2_out, NOT_R_OUT);
  Register register_1 (.D(BUS_IN), .en(not_1_out), .clk(CLK), .Q(ASYNC_OUT), .clr(1'b0));
  assign BUS_OUT = not_2_out ? ASYNC_OUT : 8'bz;  // Controlled_Buffer controlled_buffer_1
endmodule

module ALUOperandSelector (
  input  X_SEL0,
  input  X_SEL1,
  input  Y_SEL0,
  input  Y_SEL1,
  input  Y_SEL2,
  input  [7:0] A_ASYNC,
  input  [7:0] B_ASYNC,
  input  [7:0] C_ASYNC,
  input  [7:0] D_ASYNC,
  input  [7:0] E_ASYNC,
  input  [7:0] F_ASYNC,
  output [7:0] O1,
  output [7:0] O2
);

  wire decoder_1_out0, decoder_1_out1, decoder_1_out2, decoder_1_out3, decoder_2_out0, decoder_2_out1,
       decoder_2_out2, decoder_2_out3, decoder_2_out4, decoder_2_out5;

  Decoder #(.select(2)) decoder_1 (
    .out0(decoder_1_out0), .out1(decoder_1_out1), .out2(decoder_1_out2), .out3(decoder_1_out3),
    .sel({X_SEL1, X_SEL0}), .en(1'b1));
  Decoder #(.select(3)) decoder_2 (
    .out0(decoder_2_out0), .out1(decoder_2_out1), .out2(decoder_2_out2), .out3(decoder_2_out3),
    .out4(decoder_2_out4), .out5(decoder_2_out5), .sel({Y_SEL2, Y_SEL1, Y_SEL0}), .en(1'b1));  // open: out6, out7
  assign O1 = decoder_1_out0 ? A_ASYNC : 8'bz;  // Controlled_Buffer controlled_buffer_1
  assign O1 = decoder_1_out1 ? B_ASYNC : 8'bz;  // Controlled_Buffer controlled_buffer_2
  assign O1 = decoder_1_out2 ? C_ASYNC : 8'bz;  // Controlled_Buffer controlled_buffer_3
  assign O1 = decoder_1_out3 ? D_ASYNC : 8'bz;  // Controlled_Buffer controlled_buffer_4
  assign O2 = decoder_2_out4 ? E_ASYNC : 8'bz;  // Controlled_Buffer controlled_buffer_5
  assign O2 = decoder_2_out5 ? F_ASYNC : 8'bz;  // Controlled_Buffer controlled_buffer_6
  assign O2 = decoder_2_out0 ? A_ASYNC : 8'bz;  // Controlled_Buffer controlled_buffer_7
  assign O2 = decoder_2_out1 ? B_ASYNC : 8'bz;  // Controlled_Buffer controlled_buffer_8
  assign O2 = decoder_2_out2 ? C_ASYNC : 8'bz;  // Controlled_Buffer controlled_buffer_9
  assign O2 = decoder_2_out3 ? D_ASYNC : 8'bz;  // Controlled_Buffer controlled_buffer_10
endmodule

module ALUOperatorSelector (
  input  OP_SEL0,
  input  OP_SEL1,
  input  OP_SEL2,
  output [7:0] OP_OUT
);

  Decoder #(.select(3)) decoder_1 (
    .out0(OP_OUT[0]), .out1(OP_OUT[1]), .out2(OP_OUT[2]), .out3(OP_OUT[3]), .out4(OP_OUT[4]),
    .out5(OP_OUT[5]), .out6(OP_OUT[6]), .out7(OP_OUT[7]), .sel({OP_SEL2, OP_SEL1, OP_SEL0}), .en(1'b1));
endmodule

module FLAGSRegister (
  input  [7:0] BUS_IN,
  input  I_VAL,
  input  [2:0] ALU_FLAGS,
  input  NOT_CZN_IN,
  input  NOT_I_IN,
  input  FLAGS_IN_SEL,
  input  CLK,
  output [3:0] FLAGS_OUT
);

  wire not_1_out, not_2_out;
  wire [3:0] multiplexer_1_out;

  Multiplexer #(.width(4)) multiplexer_1 (
    .in0(BUS_IN[3:0]), .in1({I_VAL, ALU_FLAGS}), .out(multiplexer_1_out), .sel(FLAGS_IN_SEL));
  Register #(.width(3)) CZN (.D(multiplexer_1_out[2:0]), .en(not_1_out), .clk(CLK), .Q(FLAGS_OUT[2:0]));  // open: clr
  not not_1 (not_1_out, NOT_CZN_IN);
  Register #(.width(1)) I (.D(multiplexer_1_out[3]), .en(not_2_out), .clk(CLK), .Q(FLAGS_OUT[3]));  // open: clr
  not not_2 (not_2_out, NOT_I_IN);
endmodule

module ALU (
  input  [7:0] OPERATORS,
  input  [7:0] O1,
  input  [7:0] O2,
  output [7:0] BUS_OUT,
  output [2:0] FLAGS
);

  wire adder_1_cout, and_2_out, and_3_out, nor_1_out, nor_2_out, nor_3_out, nor_4_out, or_2_out;
  wire [6:0] buffer_1_out;
  wire [7:0] adder_1_out, and_1_out, bit_extender_1_out, not_1_out, or_1_out, xor_1_out, xor_2_out;

  assign not_1_out = ~O1;  // NOT_Gate not_1, 8 bits wide
  assign xor_1_out = O1 ^ O2;  // XOR_Gate xor_1, 8 bits wide
  assign BUS_OUT = OPERATORS[6] ? not_1_out : 8'bz;  // Controlled_Buffer controlled_buffer_1
  assign BUS_OUT = OPERATORS[5] ? xor_1_out : 8'bz;  // Controlled_Buffer controlled_buffer_2
  assign and_1_out = O1 & O2;  // AND_Gate and_1, 8 bits wide
  assign BUS_OUT = OPERATORS[4] ? and_1_out : 8'bz;  // Controlled_Buffer controlled_buffer_3
  // NoConnect on OPERATORS[7]
  assign or_1_out = O1 | O2;  // OR_Gate or_1, 8 bits wide
  assign BUS_OUT = OPERATORS[3] ? or_1_out : 8'bz;  // Controlled_Buffer controlled_buffer_4
  nor nor_1 (nor_1_out, FLAGS[2], buffer_1_out[6]);
  assign bit_extender_1_out = {{7{OPERATORS[2]}}, OPERATORS[2]};  // Bit_Extender bit_extender_1
  assign {FLAGS[2], buffer_1_out} = BUS_OUT;  // Buffer buffer_1, 8 bits wide
  Pull_Resistor pull_resistor_1 (.node({FLAGS[2], buffer_1_out}));
  nor nor_2 (nor_2_out, buffer_1_out[5], buffer_1_out[4]);
  nor nor_3 (nor_3_out, buffer_1_out[3], buffer_1_out[2]);
  and and_2 (and_2_out, nor_1_out, nor_2_out);
  and and_3 (and_3_out, nor_3_out, nor_4_out);
  and and_4 (FLAGS[1], and_2_out, and_3_out);
  Adder adder_1 (.a(O1), .b(xor_2_out), .out(adder_1_out), .cin(OPERATORS[2]), .cout(adder_1_cout));
  assign xor_2_out = O2 ^ bit_extender_1_out;  // XOR_Gate xor_2, 8 bits wide
  assign BUS_OUT = or_2_out ? adder_1_out : 8'bz;  // Controlled_Buffer controlled_buffer_5
  xor xor_3 (FLAGS[0], OPERATORS[2], adder_1_cout);
  nor nor_4 (nor_4_out, buffer_1_out[1], buffer_1_out[0]);
  or or_2 (or_2_out, OPERATORS[2], OPERATORS[1]);

  // Notes on the sheet:
  //   we invert the carry when subtracting, so that the carry flag in a sub operation means "borrow"
endmodule

module ClockModule (
  input  NOT_HLT,
  output C2,
  output C1,
  output C4,
  output C3
);

  wire CLK_GEN_out, sysclk_out;

  Clock #(.highDuration(2), .lowDuration(2), .phaseOffset(3)) CLK_GEN (.out(CLK_GEN_out));
  Clock #(.highDuration(2), .lowDuration(2)) sysclk (.out(sysclk_out));
  and and_1 (C2, CLK_GEN_out, NOT_HLT);
  and and_2 (C1, NOT_HLT, sysclk_out);
  not not_1 (C4, C2);
  not not_2 (C3, C1);
endmodule

module InstructionRegister (
);

  Counter counter_1 ();  // open: clr, load, up, count, clk, D, carry, Q
endmodule

module RAMModule (
  input  NOT_PUSH,
  input  NOT_DEVICE_IN,
  input  [7:0] BUS_IN,
  input  NOT_DEVICE_SEL_RAM,
  input  [7:0] SP,
  input  NOT_DEVICE_OUT,
  input  NOT_POP,
  input  CLK,
  input  [7:0] SS,
  input  [15:0] ABUS,
  output [7:0] BUS_OUT
);

  wire nand_1_out, nand_2_out, nand_3_out, nand_4_out, nand_5_out, nand_6_out, nand_7_out, not_1_out,
       not_2_out;
  wire [7:0] multiplexer_1_out, multiplexer_2_out, ram_1_data;

  Multiplexer #(.width(8)) multiplexer_1 (.in0(ABUS[7:0]), .in1(SP), .out(multiplexer_1_out), .sel(nand_1_out));
  Multiplexer #(.width(8)) multiplexer_2 (
    .in0({3'b000, ABUS[12:8]}), .in1(SS), .out(multiplexer_2_out), .sel(nand_1_out));
  RAM #(.addrWidth(13), .asyncread("true"), .databus("bidir")) ram_1 (
    .addr({multiplexer_2_out[4:0], multiplexer_1_out}), .we(not_1_out), .oe(not_2_out), .clk(CLK),
    .data(ram_1_data));
  nand nand_1 (nand_1_out, NOT_PUSH, NOT_POP);
  not not_1 (not_1_out, nand_2_out);
  assign ram_1_data = not_1_out ? BUS_IN : 8'bz;  // Controlled_Buffer controlled_buffer_1
  nand nand_2 (nand_2_out, nand_4_out, nand_5_out);
  not not_2 (not_2_out, nand_3_out);
  nand nand_3 (nand_3_out, nand_6_out, nand_7_out);
  assign BUS_OUT = not_2_out ? ram_1_data : 8'bz;  // Controlled_Buffer controlled_buffer_2
  nand nand_4 (nand_4_out, NOT_PUSH, NOT_DEVICE_IN);
  nand nand_5 (nand_5_out, NOT_DEVICE_SEL_RAM, NOT_PUSH);
  nand nand_6 (nand_6_out, NOT_DEVICE_SEL_RAM, NOT_POP);
  nand nand_7 (nand_7_out, NOT_DEVICE_OUT, NOT_POP);
endmodule

module StackPointer (
  input  NOT_SP_IN,
  input  SP_DIR,
  input  NOT_SP_CT,
  input  CLK,
  output [7:0] SP_OUT
);

  wire not_1_out, not_2_out;

  not not_1 (not_1_out, NOT_SP_IN);
  Counter counter_1 (
    .clr(1'b0), .load(not_1_out), .up(SP_DIR), .count(not_2_out), .clk(CLK), .D({8{1'b0}}), .Q(SP_OUT));  // open: carry
  not not_2 (not_2_out, NOT_SP_CT);
endmodule

module ROMModule (
  input  [15:0] ABUS,
  input  [12:0] CS_PC,
  input  ROM_AS,
  input  CLK,
  input  NOT_DEVICE_SEL_ROM,
  input  NOT_DEVICE_OUT,
  input  NOT_FETCH,
  output [7:0] BUS_OUT,
  output [7:0] IR_OUT
);

  wire nand_1_out, nand_2_out, not_1_out, not_2_out, or_1_out;
  wire [7:0] STORAGE_ROM_data;
  wire [12:0] multiplexer_1_out;

  nand nand_1 (nand_1_out, ROM_AS, 1'b1);
  Multiplexer #(.width(13)) multiplexer_1 (.in0(ABUS[12:0]), .in1(CS_PC), .out(multiplexer_1_out), .sel(nand_2_out));
  nand nand_2 (nand_2_out, CLK, nand_1_out);
  ROM #(.addrWidth(13)) STORAGE_ROM (.addr(multiplexer_1_out), .data(STORAGE_ROM_data));
  not not_1 (not_1_out, or_1_out);
  or or_1 (or_1_out, NOT_DEVICE_SEL_ROM, NOT_DEVICE_OUT);
  assign BUS_OUT = not_1_out ? STORAGE_ROM_data : 8'bz;  // Controlled_Buffer controlled_buffer_1
  assign IR_OUT = not_2_out ? STORAGE_ROM_data : 8'bz;  // Controlled_Buffer controlled_buffer_2
  not not_2 (not_2_out, NOT_FETCH);

  // Notes on the sheet:
  //   This way we ensure that ROM_AS is 1 during data latch (consult timing diagram)
  //   contents of STORAGE_ROM (hex, n*v repeats v):
  //   0 0 8 1 5 1f ca 1f ff 0 bb b6 df b e9 da 37 e8 90 20 df 28 90 a df 33 e5 0 45 90 ff df b 4*db 58 e0
  //   b 47 1e ff 20 d6 1a ff 51 bb e0 b 47 1e ff bb b6 df 3f da 25 58 e0 37 51 3b 60 0 e0 7 7c 30 de 63 90
  //   9 de 68 df 68 7c 11 de 63 90 5 de 66 df 66 7c 20 de 63 90 5 de 66 df 66 4 ff e6 68 a e6 7831*0 44 3f
  //   40 0 a7 df d 3f 40 1 32 d6 4e e7
endmodule

module CodeSegment_ProgramCounter (
  input  [3:0] FLAGS,
  input  J,
  input  JC,
  input  JZ,
  input  JN,
  input  JA,
  input  NOT_PC_IN,
  input  NOT_CS_IN,
  input  NOT_PC_INC,
  input  RESET,
  input  [15:0] ABUS,
  input  CLK,
  input  NOT_PC_OUT,
  input  NOT_CS_OUT,
  input  CSPC_DIR,
  output [12:0] CS_PC,
  output [7:0] BUS_OUT
);

  wire and_1_out, and_2_out, and_3_out, and_4_out, and_5_out, nor_1_out, nor_2_out, nor_3_out, not_1_out,
       not_2_out, not_3_out, or_1_out, or_2_out, or_3_out, or_4_out, PC_carry;
  wire [7:5] CS_q;

  and and_1 (and_1_out, JC, FLAGS[0]);
  or or_1 (or_1_out, and_1_out, and_2_out);
  and and_2 (and_2_out, JZ, FLAGS[1]);
  and and_3 (and_3_out, JN, FLAGS[2]);
  or or_2 (or_2_out, and_3_out, and_4_out);
  or or_3 (or_3_out, or_1_out, or_2_out);
  nor nor_1 (nor_1_out, J, or_3_out);
  and and_4 (and_4_out, JA, FLAGS[3]);
  nor nor_2 (nor_2_out, NOT_CS_IN, nor_1_out);
  and and_5 (and_5_out, CLK, or_4_out);
  or or_4 (or_4_out, RESET, CS_q[5]);
  not not_1 (not_1_out, NOT_PC_OUT);
  not not_2 (not_2_out, NOT_CS_OUT);
  Counter CS (
    .clr(and_5_out), .load(nor_2_out), .up(CSPC_DIR), .count(PC_carry), .clk(CLK), .D(ABUS[15:8]),
    .Q({CS_q, CS_PC[12:8]}));  // open: carry
  not not_3 (not_3_out, NOT_PC_INC);
  nor nor_3 (nor_3_out, nor_1_out, NOT_PC_IN);
  Counter PC (
    .clr(and_5_out), .load(nor_3_out), .up(CSPC_DIR), .count(not_3_out), .clk(CLK), .D(ABUS[7:0]),
    .carry(PC_carry), .Q(CS_PC[7:0]));
  assign BUS_OUT = not_2_out ? {CS_q, CS_PC[12:8]} : 8'bz;  // Controlled_Buffer controlled_buffer_1
  assign BUS_OUT = not_1_out ? CS_PC[7:0] : 8'bz;  // Controlled_Buffer controlled_buffer_2
endmodule

module LCD_emulator (
  input  RS,
  input  R_NW,
  input  LCD_EN,
  input  [7:0] BUS_IN
);
endmodule

module Interface_emulator (
  input  POLL,
  input  TRANSMIT,
  input  CLK,
  input  [7:0] BUS_IN,
  output [7:0] BUS_OUT,
  output A_OUT
);

  wire [7:0] register_1_q;

  Register register_1 (.D(BUS_IN), .en(TRANSMIT), .clk(CLK), .Q(register_1_q));  // open: clr
  assign BUS_OUT = POLL ? register_1_q : 8'bz;  // Controlled_Buffer controlled_buffer_1

  assign A_OUT = POLL;
endmodule

module ControlUnit (
  input  [7:0] DATA_LATCH,
  input  NOT_IRQ,
  input  CLK90,
  input  RESET,
  input  I,
  output NOT_RA_IN,
  output NOT_RA_OUT,
  output NOT_RA_SL,
  output NOT_RA_SR,
  output NOT_RB_IN,
  output NOT_RB_OUT,
  output NOT_RC_IN,
  output NOT_RC_OUT,
  output NOT_RD_IN,
  output NOT_RD_OUT,
  output NOT_DEVICE_IN,
  output NOT_DEVICE_OUT,
  output NOT_SS_IN,
  output NOT_SP_IN,
  output NOT_SP_CT,
  output SP_DIR,
  output NOT_ABH_IN,
  output NOT_ABL_IN,
  output NOT_RT_IN,
  output NOT_RT_OUT,
  output X_SEL0,
  output X_SEL1,
  output Y_SEL0,
  output Y_SEL1,
  output Y_SEL2,
  output OP_SEL0,
  output OP_SEL1,
  output OP_SEL2,
  output ROM_AS,
  output NOT_CS_IN,
  output NOT_PC_IN,
  output NOT_PC_INC,
  output NOT_CS_OUT,
  output NOT_PC_OUT,
  output NOT_FETCH,
  output J,
  output JC,
  output JZ,
  output JN,
  output JA,
  output NOT_PASS,
  output NOT_HLT,
  output PAGE_0,
  output NOT_PUSH,
  output NOT_POP,
  output NOT_DATA_LATCH_OUT,
  output NOT_IVH_OUT,
  output NOT_IVL_OUT,
  output I_VAL,
  output FLAGS_MODE_SEL0,
  output FLAGS_MODE_SEL1,
  output NOT_FLAGS_OUT,
  output CSPC_DIR
);

  wire and_1_out, edgedetector_1_pulse, not_1_out, or_1_out, or_2_out;
  wire [3:0] counter_1_q;
  wire [7:0] IR_q, multiplexer_1_out;
  wire [7:5] EEPROM6_data;

  not not_1 (not_1_out, NOT_PASS);
  Multiplexer #(.width(8)) multiplexer_1 (.in0(8'h2), .in1(DATA_LATCH), .out(multiplexer_1_out), .sel(or_1_out));
  or or_1 (or_1_out, NOT_IRQ, I);
  or or_2 (or_2_out, not_1_out, RESET);
  EdgeDetector edgedetector_1 (.D(CLK90), .PULSE(edgedetector_1_pulse));
  Register IR (.D(multiplexer_1_out), .en(or_2_out), .clk(CLK90), .Q(IR_q), .clr(RESET));
  Counter #(.max('hf), .width(4)) counter_1 (
    .clr(and_1_out), .load(1'b0), .up(1'b1), .count(1'b1), .clk(CLK90), .D(4'b1111), .Q(counter_1_q));  // open: carry
  and and_1 (and_1_out, or_2_out, edgedetector_1_pulse);
  ROM #(.addrWidth(13)) EEPROM0 (
    .addr({1'b0, IR_q, counter_1_q}),
    .data({NOT_RC_OUT, NOT_RC_IN, NOT_RB_OUT, NOT_RB_IN, NOT_RA_SR, NOT_RA_SL, NOT_RA_OUT, NOT_RA_IN}));
  ROM #(.addrWidth(13)) EEPROM1 (
    .addr({1'b0, IR_q, counter_1_q}),
    .data({SP_DIR, NOT_SP_CT, NOT_SP_IN, NOT_SS_IN, NOT_DEVICE_OUT, NOT_DEVICE_IN, NOT_RD_OUT, NOT_RD_IN}));
  ROM #(.addrWidth(13)) EEPROM2 (
    .addr({1'b0, IR_q, counter_1_q}),
    .data({Y_SEL1, Y_SEL0, X_SEL1, X_SEL0, NOT_RT_OUT, NOT_RT_IN, NOT_ABL_IN, NOT_ABH_IN}));
  ROM #(.addrWidth(13)) EEPROM3 (
    .addr({1'b0, IR_q, counter_1_q}),
    .data({NOT_PC_INC, NOT_PC_IN, NOT_CS_IN, ROM_AS, OP_SEL2, OP_SEL1, OP_SEL0, Y_SEL2}));
  ROM #(.addrWidth(13)) EEPROM4 (
    .addr({1'b0, IR_q, counter_1_q}), .data({JA, JN, JZ, JC, J, NOT_FETCH, NOT_PC_OUT, NOT_CS_OUT}));
  ROM #(.addrWidth(13)) EEPROM5 (
    .addr({1'b0, IR_q, counter_1_q}),
    .data({NOT_IVL_OUT, NOT_IVH_OUT, NOT_DATA_LATCH_OUT, NOT_POP, NOT_PUSH, PAGE_0, NOT_HLT, NOT_PASS}));
  ROM #(.addrWidth(13)) EEPROM6 (
    .addr({1'b0, IR_q, counter_1_q}),
    .data({EEPROM6_data, CSPC_DIR, NOT_FLAGS_OUT, FLAGS_MODE_SEL1, FLAGS_MODE_SEL0, I_VAL}));

  // Notes on the sheet:
  //   Get the 163! Synchronous reset
  //   contents of EEPROM0 (hex, n*v repeats v):
  //   48*ff fe 15*ff ef 15*ff bf 63*ff ed 15*ff bd 15*ff fd 15*ff de 15*ff 9f 15*ff df 15*ff 7e 15*ff 6f
  //   15*ff 7f 15*ff fe 15*ff ef 15*ff bf 48*ff fd 15*ff df 15*ff 7f 31*ff fe 15*ff ef 15*ff bf 47*ff fd
  //   15*ff df 15*ff 7f 31*ff fe 15*ff ef 15*ff bf 48*ff fd 15*ff df 15*ff 7f 31*ff fe 15*ff ef 15*ff bf
  //   45*ff 7f ff fd 13*ff 7f ff df 13*ff 7f ff 7f 13*ff 7f 15*ff 7f ff fe 13*ff 7f ff ef 13*ff 7f ff bf
  //   13*ff 7f 15*ff 7f 17*ff fd 15*ff df 15*ff 7f 31*ff fe 15*ff ef 15*ff bf 45*ff fd 15*ff df 15*ff 7f
  //   79*ff 7f 47*ff fe 15*ff ef 15*ff bf 80*ff 7f 31*ff fe 15*ff fe 15*ff fe 15*ff fe 14*ff ef 15*ff ef
  //   15*ff ef 15*ff ef 15*ff bf 15*ff bf 15*ff bf 15*ff bf 81*ff fe 14*ff ef 15*ff ef 15*ff ef 15*ff fe
  //   15*ff fe 15*ff fe 15*ff fe 14*ff ef 15*ff ef 15*ff ef 15*ff ef 15*ff bf 15*ff bf 15*ff bf 15*ff bf
  //   81*ff fe 14*ff ef 15*ff ef 15*ff ef 335*ff fe 15*ff fe 15*ff fe 15*ff fe 14*ff ef 15*ff ef 15*ff ef
  //   15*ff ef 15*ff bf 15*ff bf 15*ff bf 15*ff bf 81*ff fe 14*ff ef 15*ff ef 15*ff ef 15*ff fe 15*ff fe
  //   15*ff fe 15*ff fe 14*ff ef 15*ff ef 15*ff ef 15*ff ef 15*ff bf 15*ff bf 15*ff bf 15*ff bf 81*ff fe
  //   14*ff ef 15*ff ef 15*ff ef 15*ff fe 15*ff fe 15*ff fe 15*ff fe 14*ff ef 15*ff ef 15*ff ef 15*ff ef
  //   15*ff bf 15*ff bf 15*ff bf 15*ff bf 81*ff fe 14*ff ef 15*ff ef 15*ff ef 15*ff fe 14*ff ef 15*ff bf
  //   32*ff fe 14*ff ef 15*ff bf 32*ff fe 14*ff ef 15*ff bf 31*ff fb 15*ff f7 15*ff fd de ef 13*ff fd 7e
  //   bf 13*ff fd fe 14*ff df 6f bf 13*ff df ef 14*ff 7f bf 222*ff
  //   contents of EEPROM1 (hex, n*v repeats v):
  //   35*7f bf bf bf 58*7f 7e 15*7f 5f 15*7f 6f 47*7f 7e 47*7f 7e 47*7f 7e 15*7f 7d 15*7f 7d 15*7f 7d
  //   15*7f 6d 15*7f 5d 16*7f 7b 15*7f 7b 15*7f 7b 15*7f 79 15*7f 77 15*7f 77 15*7f 77 15*7f 76 15*7f 7b
  //   14*7f 7d 7b 14*7f 7d 7b 14*7f 7d 7b 14*7f 7d 79 14*7f 7d 77 14*7f 7d 77 14*7f 7d 77 14*7f 7d 76
  //   14*7f 7d 7b 15*7f 7d 7b 14*7f 7d 7b 14*7f 7d 7b 14*7f 7d 79 14*7f 7d 77 14*7f 7d 77 14*7f 7d 77
  //   14*7f 7d 76 14*7f 7d 7b 14*7f 7d 7b 14*7f 7d 7b 14*7f 7d 7b 14*7f 7d 79 14*7f 7d 77 14*7f 7d 77
  //   14*7f 7d 77 14*7f 7d 76 14*7f 7d 7b 15*7f 7b 15*7f 7b 15*7f 7b 15*7f 79 15*7f 77 15*7f 77 15*7f 77
  //   15*7f 76 15*7f 7b 14*7f bf 15*7f bf 15*7f bf 14*7f 7d bf 15*7f 77 7f bf 12*7f 7d 77 7f bf 13*7f 7d
  //   77 7f bf 12*7f 7d 77 7f bf 12*7f 7d 77 7f bf 12*7f bf 14*7f 3f 15*7f 3f 15*7f 3f 15*7f 3e 16*7f 3f
  //   7b 13*7f 7d 3f 7b 13*7f 3f 7f 7d 7b 12*7f 3f 7f 7d 7b 12*7f 3f 7f 7d 7b 204*7f 7e 15*7f 7e 15*7f 7e
  //   15*7f 7e 271*7f 7e 15*7f 7e 15*7f 7e 15*7f 7e 591*7f 7e 15*7f 7e 15*7f 7e 15*7f 7e 271*7f 7e 15*7f
  //   7e 15*7f 7e 15*7f 7e 271*7f 7e 15*7f 7e 15*7f 7e 15*7f 7e 127*7f 7e 63*7f 7e 63*7f 7e 80*7f 7d 7e
  //   30*7f 7d 7e 14*7f 7d 7e 144*7f bf bf 11*7f 3f 3f 14*7f 3f 3f 3f 45*7f
  //   contents of EEPROM2 (hex, n*v repeats v):
  //   32*f e d 334*f d 15*f d 15*f d 15*f d 15*f d 15*f d 15*f d 15*f d 15*f d 15*f d 15*f d 15*f d 15*f d
  //   15*f d 15*f d 15*f d 15*f d 15*f d 15*f e d 14*f e d 14*f e d 14*f e d 14*f e d 14*f e d 14*f e d
  //   14*f e d 14*f e d 14*f e d 14*f e d 14*f e d 14*f e d 14*f e d 14*f e d 14*f e d 14*f e d 14*f e d
  //   14*f e d 14*f e d 14*f e d 14*f e d 14*f e d 14*f e d 14*f e d 14*f e d 14*f e d 78*f d b 7 13*f d b
  //   7 13*f e d b 7 12*f e d b 7 12*f e d b 7 92*f d b 7 13*f d b 7 13*f b e d 7 12*f b e d 7 12*f b e d
  //   7 12*f b 7 14*f 4b 7 14*f 8b 7 14*f cb 7 14*f 1f 15*f 5f 15*f 9f 15*f df 15*f 2f 15*f 6f 15*f af
  //   15*f ef 15*f 3f 15*f 7f 15*f bf 15*f ff 15*f b b 7 13*f b 1f 14*f b 2f 14*f b 3f 14*f b 7 14*f 4b 7
  //   14*f 8b 7 14*f cb 7 14*f 1f 15*f 5f 15*f 9f 15*f df 15*f 2f 15*f 6f 15*f af 15*f ef 15*f 3f 15*f 7f
  //   15*f bf 15*f ff 15*f b b 7 13*f b 1f 14*f b 2f 14*f b 3f 30*f 4f 15*f 8f 15*f cf 15*f 1f 15*f 5f
  //   15*f 9f 15*f df 15*f 2f 15*f 6f 15*f af 15*f ef 15*f 3f 15*f 7f 15*f bf 15*f ff 15*f b 15*f b 1f
  //   14*f b 2f 14*f b 3f 14*f b 7 14*f 4b 7 14*f 8b 7 14*f cb 7 14*f 1f 15*f 5f 15*f 9f 15*f df 15*f 2f
  //   15*f 6f 15*f af 15*f ef 15*f 3f 15*f 7f 15*f bf 15*f ff 15*f b b 7 13*f b 1f 14*f b 2f 14*f b 3f
  //   14*f b 7 14*f 4b 7 14*f 8b 7 14*f cb 7 14*f 1f 15*f 5f 15*f 9f 15*f df 15*f 2f 15*f 6f 15*f af 15*f
  //   ef 15*f 3f 15*f 7f 15*f bf 15*f ff 15*f b b 7 13*f b 1f 14*f b 2f 14*f b 3f 14*f b 7 14*f 4b 7 14*f
  //   8b 7 14*f cb 7 14*f 1f 15*f 5f 15*f 9f 15*f df 15*f 2f 15*f 6f 15*f af 15*f ef 15*f 3f 15*f 7f 15*f
  //   bf 15*f ff 15*f b b 7 13*f b 1f 14*f b 2f 14*f b 3f 14*f b 7 14*f 1f 15*f 2f 15*f 3f 15*f 4b 7 14*f
  //   5f 15*f 6f 15*f 7f 15*f 4b 7 14*f 5f 15*f 6f 15*f 7f 47*f b f 7 13*f b f 7 13*f b f 7 13*f b f 7
  //   13*f b f 7 13*f b f 7 13*f d 15*f d 15*f d 15*f d 15*f e d 14*f e d 14*f e d 14*f e d 14*f e d 14*f
  //   d e 15*f d e 45*f
  //   contents of EEPROM3 (hex, n*v repeats v):
  //   60 15*e0 60 15*e0 60 4*e0 80 60 9*e0 60 60 14*e0 60 60 14*e0 60 60 14*e0 60 60 14*e0 60 60 14*e0 60
  //   60 14*e0 60 15*e0 60 15*e0 60 15*e0 60 15*e0 60 15*e0 60 15*e0 60 15*e0 60 15*e0 60 15*e0 60 15*e0
  //   60 15*e0 60 15*e0 60 15*e0 60 15*e0 60 60 14*e0 60 60 14*e0 60 60 14*e0 60 60 14*e0 60 60 14*e0 60
  //   60 14*e0 60 60 14*e0 60 60 14*e0 60 60 60 14*e0 60 15*e0 60 15*e0 60 15*e0 60 15*e0 60 15*e0 60
  //   15*e0 60 15*e0 60 15*e0 60 60 13*e0 60 e0 60 13*e0 60 e0 60 13*e0 60 e0 60 13*e0 60 e0 60 13*e0 60
  //   e0 60 13*e0 60 e0 60 13*e0 60 e0 60 13*e0 60 e0 60 13*e0 60 e0 60 60 14*e0 60 15*e0 60 15*e0 60
  //   15*e0 60 15*e0 60 15*e0 60 15*e0 60 15*e0 60 15*e0 60 60 12*e0 60 60 60 13*e0 60 60 60 13*e0 60 60
  //   60 13*e0 60 60 60 13*e0 60 60 60 13*e0 60 60 60 13*e0 60 60 60 13*e0 60 60 60 13*e0 4*60 13*e0 60
  //   15*e0 60 15*e0 60 15*e0 60 14*e0 60 e0 e0 60 15*e0 60 12*e0 60 e0 e0 e0 60 15*e0 60 11*e0 60 e0 e0
  //   e0 60 11*e0 60 60 14*e0 60 15*e0 60 15*e0 60 15*e0 60 15*e0 60 e0 60 15*e0 60 14*e0 60 e0 60 15*e0
  //   60 13*e0 60 e0 60 12*e0 e2 60 14*e0 e2 60 14*e0 e2 60 14*e0 e2 60 14*e0 62 15*e0 62 15*e0 62 15*e0
  //   62 15*e0 62 15*e0 62 15*e0 62 15*e0 62 15*e0 62 15*e0 62 15*e0 62 15*e0 62 15*e0 60 e3 60 13*e0 60
  //   63 14*e0 60 63 14*e0 60 63 14*e0 e4 60 14*e0 e4 60 14*e0 e4 60 14*e0 e4 60 14*e0 64 15*e0 64 15*e0
  //   64 15*e0 64 15*e0 64 15*e0 64 15*e0 64 15*e0 64 15*e0 64 15*e0 64 15*e0 64 15*e0 64 15*e0 60 e5 60
  //   13*e0 60 65 14*e0 60 65 14*e0 60 65 14*e0 64 15*e0 64 15*e0 64 15*e0 64 15*e0 64 15*e0 64 15*e0 64
  //   15*e0 64 15*e0 64 15*e0 64 15*e0 64 15*e0 64 15*e0 64 15*e0 64 15*e0 64 15*e0 64 15*e0 60 65 14*e0
  //   60 65 14*e0 60 65 14*e0 60 65 14*e0 e6 60 14*e0 e6 60 14*e0 e6 60 14*e0 e6 60 14*e0 66 15*e0 66
  //   15*e0 66 15*e0 66 15*e0 66 15*e0 66 15*e0 66 15*e0 66 15*e0 66 15*e0 66 15*e0 66 15*e0 66 15*e0 60
  //   e7 60 13*e0 60 67 14*e0 60 67 14*e0 60 67 14*e0 e8 60 14*e0 e8 60 14*e0 e8 60 14*e0 e8 60 14*e0 68
  //   15*e0 68 15*e0 68 15*e0 68 15*e0 68 15*e0 68 15*e0 68 15*e0 68 15*e0 68 15*e0 68 15*e0 68 15*e0 68
  //   15*e0 60 e9 60 13*e0 60 69 14*e0 60 69 14*e0 60 69 14*e0 ea 60 14*e0 ea 60 14*e0 ea 60 14*e0 ea 60
  //   14*e0 6a 15*e0 6a 15*e0 6a 15*e0 6a 15*e0 6a 15*e0 6a 15*e0 6a 15*e0 6a 15*e0 6a 15*e0 6a 15*e0 6a
  //   15*e0 6a 15*e0 60 eb 60 13*e0 60 6b 14*e0 60 6b 14*e0 60 6b 14*e0 ec 60 14*e0 6c 15*e0 6c 15*e0 6c
  //   15*e0 e3 60 14*e0 63 15*e0 63 15*e0 63 15*e0 e5 60 14*e0 65 15*e0 65 15*e0 65 15*e0 60 15*e0 60
  //   17*e0 60 15*e0 60 15*e0 60 15*e0 60 15*e0 60 15*e0 60 13*e0 60 a0 60 13*e0 60 a0 60 13*e0 60 a0 60
  //   13*e0 60 a0 60 13*e0 60 60 80 60 12*e0 60 60 80 60 12*e0 60 60 80 60 12*e0 60 60 80 60 12*e0 60 60
  //   e0 e0 80 60 12*e0 80 60 15*e0 80 60 11*e0 60 15*e0 60 15*e0
  //   contents of EEPROM4 (hex, n*v repeats v):
  //   3 15*7 3 17*7 6 5 7 f 3 9*7 3 3 14*7 3 3 14*7 3 3 14*7 3 3 14*7 3 3 14*7 3 3 14*7 3 15*7 3 15*7 3
  //   15*7 3 15*7 3 15*7 3 15*7 3 15*7 3 15*7 3 15*7 3 15*7 3 15*7 3 15*7 3 15*7 3 15*7 3 3 14*7 3 3 14*7
  //   3 3 14*7 3 3 14*7 3 3 14*7 3 3 14*7 3 3 14*7 3 3 14*7 3 3 3 14*7 3 15*7 3 15*7 3 15*7 3 15*7 3 15*7
  //   3 15*7 3 15*7 3 15*7 3 3 13*7 3 7 3 13*7 3 7 3 13*7 3 7 3 13*7 3 7 3 13*7 3 7 3 13*7 3 7 3 13*7 3 7
  //   3 13*7 3 7 3 13*7 3 7 3 3 14*7 3 15*7 3 15*7 3 15*7 3 15*7 3 15*7 3 15*7 3 15*7 3 15*7 3 3 12*7 3 3
  //   3 13*7 3 3 3 13*7 3 3 3 13*7 3 3 3 13*7 3 3 3 13*7 3 3 3 13*7 3 3 3 13*7 3 3 3 13*7 4*3 13*7 3 15*7
  //   3 15*7 3 15*7 3 14*7 3 7 7 3 15*7 3 12*7 3 7 7 7 3 15*7 3 11*7 3 7 7 7 3 11*7 3 3 14*7 3 15*7 3 15*7
  //   3 15*7 3 15*7 3 7 3 15*7 3 14*7 3 7 3 15*7 3 13*7 3 7 3 13*7 3 15*7 3 15*7 3 15*7 3 14*7 3 15*7 3
  //   15*7 3 15*7 3 15*7 3 15*7 3 15*7 3 15*7 3 15*7 3 15*7 3 15*7 3 15*7 3 15*7 3 7 3 13*7 3 3 14*7 3 3
  //   14*7 3 3 15*7 3 15*7 3 15*7 3 15*7 3 14*7 3 15*7 3 15*7 3 15*7 3 15*7 3 15*7 3 15*7 3 15*7 3 15*7 3
  //   15*7 3 15*7 3 15*7 3 15*7 3 7 3 13*7 3 3 14*7 3 3 14*7 3 3 14*7 3 15*7 3 15*7 3 15*7 3 15*7 3 15*7 3
  //   15*7 3 15*7 3 15*7 3 15*7 3 15*7 3 15*7 3 15*7 3 15*7 3 15*7 3 15*7 3 15*7 3 3 14*7 3 3 14*7 3 3
  //   14*7 3 3 15*7 3 15*7 3 15*7 3 15*7 3 14*7 3 15*7 3 15*7 3 15*7 3 15*7 3 15*7 3 15*7 3 15*7 3 15*7 3
  //   15*7 3 15*7 3 15*7 3 15*7 3 7 3 13*7 3 3 14*7 3 3 14*7 3 3 15*7 3 15*7 3 15*7 3 15*7 3 14*7 3 15*7 3
  //   15*7 3 15*7 3 15*7 3 15*7 3 15*7 3 15*7 3 15*7 3 15*7 3 15*7 3 15*7 3 15*7 3 7 3 13*7 3 3 14*7 3 3
  //   14*7 3 3 15*7 3 15*7 3 15*7 3 15*7 3 14*7 3 15*7 3 15*7 3 15*7 3 15*7 3 15*7 3 15*7 3 15*7 3 15*7 3
  //   15*7 3 15*7 3 15*7 3 15*7 3 7 3 13*7 3 3 14*7 3 3 14*7 3 3 15*7 3 14*7 3 15*7 3 15*7 3 16*7 3 14*7 3
  //   15*7 3 15*7 3 16*7 3 14*7 3 15*7 3 15*7 3 15*7 3 15*7 3 17*7 3 15*7 3 15*7 3 15*7 3 15*7 3 15*7 3
  //   13*7 3 17 3 13*7 3 47 3 13*7 3 27 3 13*7 3 f 3 13*7 3 3 17 3 12*7 3 3 47 3 12*7 3 3 27 3 12*7 3 3 f
  //   3 12*7 3 3 6 5 f 3 12*7 f 3 15*7 f 3 11*7 3 15*7 3 15*7
  //   contents of EEPROM5 (hex, n*v repeats v):
  //   fa 15*fb f8 15*fb bb 7b f3 f3 f3 fb fa 9*fb db fa 14*fb db fa 14*fb db fa 14*fb db fa 14*fb db fa
  //   14*fb db fa 14*fb fa 15*fb fa 15*fb fa 15*fb fa 15*fb fa 15*fb fa 15*fb fa 15*fb fa 15*fb fa 15*fb
  //   fa 15*fb fa 15*fb fa 15*fb fa 15*fb fa 15*fb db fe 14*fb db fe 14*fb db fe 14*fb db fe 14*fb db fe
  //   14*fb db fe 14*fb db fe 14*fb db fe 14*fb db df fa 14*fb fe 15*fb fe 15*fb fe 15*fb fe 15*fb fe
  //   15*fb fe 15*fb fe 15*fb fe 15*fb df fa 13*fb db fb fa 13*fb db fb fa 13*fb db fb fa 13*fb db fb fa
  //   13*fb db fb fa 13*fb db fb fa 13*fb db fb fa 13*fb db fb fa 13*fb db fb db fa 14*fb fa 15*fb fa
  //   15*fb fa 15*fb fa 15*fb fa 15*fb fa 15*fb fa 15*fb fa 15*fb db fa 12*fb db db fa 13*fb db db fa
  //   13*fb db db fa 13*fb db db fa 13*fb db db fa 13*fb db db fa 13*fb db db fa 13*fb db db fa 13*fb db
  //   db db fa 12*fb f3 fa 14*fb f3 fa 14*fb f3 fa 14*fb f3 fa 14*fb db ff f3 fa 13*fb ff f3 fa 12*fb db
  //   fb fb f3 fa 14*fb f3 fa 11*fb db fb fb f3 fa 11*fb d3 fa 14*fb ea 15*fb ea 15*fb ea 15*fb ea 15*fb
  //   db eb fe 14*fb eb fe 13*fb eb db fb fa 12*fb eb fb fb fa 12*fb eb db fb fa 13*fb fa 15*fb fa 15*fb
  //   fa 15*fb fa 14*fb fa 15*fb fa 15*fb fa 15*fb fa 15*fb fa 15*fb fa 15*fb fa 15*fb fa 15*fb fa 15*fb
  //   fa 15*fb fa 15*fb fa 15*fb db fb fa 13*fb db fa 14*fb db fa 14*fb db fa 15*fb fa 15*fb fa 15*fb fa
  //   15*fb fa 14*fb fa 15*fb fa 15*fb fa 15*fb fa 15*fb fa 15*fb fa 15*fb fa 15*fb fa 15*fb fa 15*fb fa
  //   15*fb fa 15*fb fa 15*fb db fb fa 13*fb db fa 14*fb db fa 14*fb db fa 14*fb fa 15*fb fa 15*fb fa
  //   15*fb fa 15*fb fa 15*fb fa 15*fb fa 15*fb fa 15*fb fa 15*fb fa 15*fb fa 15*fb fa 15*fb fa 15*fb fa
  //   15*fb fa 15*fb fa 15*fb db fa 14*fb db fa 14*fb db fa 14*fb db fa 15*fb fa 15*fb fa 15*fb fa 15*fb
  //   fa 14*fb fa 15*fb fa 15*fb fa 15*fb fa 15*fb fa 15*fb fa 15*fb fa 15*fb fa 15*fb fa 15*fb fa 15*fb
  //   fa 15*fb fa 15*fb db fb fa 13*fb db fa 14*fb db fa 14*fb db fa 15*fb fa 15*fb fa 15*fb fa 15*fb fa
  //   14*fb fa 15*fb fa 15*fb fa 15*fb fa 15*fb fa 15*fb fa 15*fb fa 15*fb fa 15*fb fa 15*fb fa 15*fb fa
  //   15*fb fa 15*fb db fb fa 13*fb db fa 14*fb db fa 14*fb db fa 15*fb fa 15*fb fa 15*fb fa 15*fb fa
  //   14*fb fa 15*fb fa 15*fb fa 15*fb fa 15*fb fa 15*fb fa 15*fb fa 15*fb fa 15*fb fa 15*fb fa 15*fb fa
  //   15*fb fa 15*fb db fb fa 13*fb db fa 14*fb db fa 14*fb db fa 15*fb fa 14*fb fa 15*fb fa 15*fb fa
  //   16*fb fa 14*fb fa 15*fb fa 15*fb fa 16*fb fa 14*fb fa 15*fb fa 15*fb fa 15*fb fa 15*fb fa 17*fb fa
  //   15*fb fa 15*fb fa 15*fb fa 15*fb fa 15*fb fa 13*fb db fb fa 13*fb db fb fa 13*fb db fb fa 13*fb db
  //   fb fa 13*fb db db fb fa 12*fb db db fb fa 12*fb db db fb fa 12*fb db db fb fa 12*fb db db f3 f3 fb
  //   fa 10*fb eb eb fb fa 12*fb eb eb eb fb fa 11*fb fa 15*fb fa 15*fb
  //   contents of EEPROM6 (hex, n*v repeats v):
  //   32*1e e 1e 1e 1e 16 1b 1354*1e 1c 15*1e 1c 15*1e 1c 15*1e 1c 15*1e 1c 15*1e 1c 15*1e 1c 15*1e 1c
  //   15*1e 1c 15*1e 1c 15*1e 1c 15*1e 1c 15*1e 1c 15*1e 1c 15*1e 1c 15*1e 1c 16*1e 1c 15*1e 1c 15*1e 1c
  //   15*1e 1c 14*1e 1c 15*1e 1c 15*1e 1c 15*1e 1c 15*1e 1c 15*1e 1c 15*1e 1c 15*1e 1c 15*1e 1c 15*1e 1c
  //   15*1e 1c 15*1e 1c 15*1e 1c 15*1e 1c 15*1e 1c 15*1e 1c 16*1e 1c 15*1e 1c 15*1e 1c 15*1e 1c 14*1e 1c
  //   15*1e 1c 15*1e 1c 15*1e 1c 15*1e 1c 15*1e 1c 15*1e 1c 15*1e 1c 15*1e 1c 15*1e 1c 15*1e 1c 15*1e 1c
  //   15*1e 1c 15*1e 1c 15*1e 1c 15*1e 1c 16*1e 1c 15*1e 1c 15*1e 1c 15*1e 1c 14*1e 1c 15*1e 1c 15*1e 1c
  //   15*1e 1c 15*1e 1c 15*1e 1c 15*1e 1c 15*1e 1c 15*1e 1c 15*1e 1c 15*1e 1c 15*1e 1c 15*1e 1c 15*1e 1c
  //   15*1e 1c 15*1e 1c 16*1e 1c 15*1e 1c 15*1e 1c 15*1e 1c 14*1e 1c 15*1e 1c 15*1e 1c 15*1e 1c 15*1e 1c
  //   15*1e 1c 15*1e 1c 15*1e 1c 15*1e 1c 15*1e 1c 15*1e 1c 15*1e 1c 15*1e 1c 15*1e 1c 15*1e 1c 15*1e 1c
  //   16*1e 1c 15*1e 1c 15*1e 1c 15*1e 1c 14*1e 1c 15*1e 1c 15*1e 1c 15*1e 1c 15*1e 1c 15*1e 1c 15*1e 1c
  //   15*1e 1c 15*1e 1c 15*1e 1c 15*1e 1c 15*1e 1c 15*1e 1c 15*1e 1c 15*1e 1c 15*1e 1c 16*1e 1c 15*1e 1c
  //   15*1e 1c 15*1e 1c 14*1e 1c 15*1e 1c 15*1e 1c 15*1e 1c 15*1e 1c 15*1e 1c 15*1e 1c 15*1e 1c 15*1e 1c
  //   15*1e 1c 15*1e 1c 15*1e 1c 303*1e 18 15*1e 1a 15*1e 1b 15*1e
endmodule

module AddrDecoder (
  input  [15:0] ABUS,
  output NOT_DEVICE_SEL_RAM,
  output NOT_DEVICE_SEL_ROM,
  output NOT_DEVICE_SEL_0,
  output NOT_DEVICE_SEL_1,
  output NOT_DEVICE_SEL_2,
  output NOT_DEVICE_SEL_3,
  output NOT_DEVICE_SEL_4,
  output NOT_DEVICE_SEL_5
);

  wire decoder_1_out0, decoder_1_out1, decoder_1_out2, decoder_1_out3, decoder_1_out4, decoder_1_out5,
       decoder_1_out6, decoder_1_out7;

  Decoder #(.select(3)) decoder_1 (
    .out0(decoder_1_out0), .out1(decoder_1_out1), .out2(decoder_1_out2), .out3(decoder_1_out3),
    .out4(decoder_1_out4), .out5(decoder_1_out5), .out6(decoder_1_out6), .out7(decoder_1_out7),
    .sel(ABUS[15:13]), .en(1'b1));
  not not_1 (NOT_DEVICE_SEL_RAM, decoder_1_out0);
  not not_2 (NOT_DEVICE_SEL_ROM, decoder_1_out1);
  not not_3 (NOT_DEVICE_SEL_0, decoder_1_out2);
  not not_4 (NOT_DEVICE_SEL_1, decoder_1_out3);
  not not_5 (NOT_DEVICE_SEL_2, decoder_1_out4);
  not not_6 (NOT_DEVICE_SEL_3, decoder_1_out5);
  not not_7 (NOT_DEVICE_SEL_4, decoder_1_out6);
  not not_8 (NOT_DEVICE_SEL_5, decoder_1_out7);
endmodule

module FLAGSController (
  input  FLAGS_MODE_SEL0,
  input  FLAGS_MODE_SEL1,
  output NOT_CZN_IN,
  output NOT_I_IN,
  output FLAGS_IN_SEL
);

  or or_1 (FLAGS_IN_SEL, FLAGS_MODE_SEL0, FLAGS_MODE_SEL1);

  assign NOT_CZN_IN = FLAGS_MODE_SEL0;
  assign NOT_I_IN = FLAGS_MODE_SEL1;

  // Notes on the sheet:
  //   0
  //   0
  //   0
  //   1
  //   1
  //   0
  //   1
  //   1
  //   SEL0 SEL1 MODE
  //   load from bus
  //   load from ALU
  //   load I
  //   nothing
endmodule
