// Logisim project Devices.circ as structural Verilog: 3 circuits, main circuit ButtonAdapter
module ButtonAdapter (
  input  BUTTON_IN,
  input  [7:0] DBUS_IN,
  input  [15:0] ABUS,
  input  NOT_DEVICE_IN,
  input  NOT_DEVICE_OUT,
  input  CLK,
  output NOT_IRQ,
  output [7:0] D_BUS_OUT
);

  wire not_1_out, not_2_out;
  wire [0:0] s_r_ff_1_q;

  S_R_Flip_Flop s_r_ff_1 (.S(BUTTON_IN), .R(not_1_out), .clk(CLK), .Q(s_r_ff_1_q[0]));  // open: reset, Qn, preset
  not not_1 (not_1_out, NOT_DEVICE_IN);
  assign NOT_IRQ = s_r_ff_1_q[0] ? 1'b0 : 1'bz;  // Controlled_Buffer controlled_buffer_1
  assign D_BUS_OUT = not_2_out ? {{7{1'b0}}, s_r_ff_1_q[0]} : 8'bz;  // Controlled_Buffer controlled_buffer_2
  not not_2 (not_2_out, NOT_DEVICE_OUT);
endmodule

module HexDisplayAdapter (
  input  [7:0] DBUS_IN,
  input  [15:0] ABUS,
  input  NOT_DEVICE_IN,
  input  NOT_DEVICE_OUT,
  input  CLK,
  output [3:0] LSB,
  output [3:0] MSB
);

  wire not_1_out;

  Register register_1 (.D(DBUS_IN), .en(not_1_out), .clk(CLK), .Q({MSB, LSB}));  // open: clr
  not not_1 (not_1_out, NOT_DEVICE_IN);
endmodule

module KeyboardAdapter (
  input  K_AVAIL,
  input  [6:0] K_DATA,
  input  [7:0] BUS_IN,
  input  [15:0] ABUS,
  input  NOT_DEVICE_IN,
  input  NOT_DEVICE_OUT,
  input  CLK,
  output NOT_IRQ,
  output [7:0] BUS_OUT,
  output K_READ_EN,
  output K_CLEAR,
  output K_CLK
);

  wire bit_extender_3_out, not_2_out, not_3_out;
  wire [7:0] bit_extender_1_out, bit_extender_2_out, multiplexer_1_out, register_1_q;

  assign bit_extender_1_out = {{1{1'b0}}, K_DATA};  // Bit_Extender bit_extender_1
  not not_1 (K_CLEAR, NOT_DEVICE_IN);
  and and_1 (K_READ_EN, not_2_out, bit_extender_3_out);
  not not_2 (not_2_out, NOT_DEVICE_OUT);
  Register register_1 (.D(bit_extender_1_out), .en(K_READ_EN), .clk(not_3_out), .Q(register_1_q));  // open: clr
  not not_3 (not_3_out, CLK);
  assign bit_extender_2_out = {{7{1'b0}}, K_AVAIL};  // Bit_Extender bit_extender_2
  Transistor #(.\type ("n")) transistor_1 (.in(1'b0), .out(NOT_IRQ), .gate(K_AVAIL));
  Bit_Extender #(.in_width(16), .out_width(1)) bit_extender_3 (.in(ABUS), .out(bit_extender_3_out));
  assign BUS_OUT = not_2_out ? multiplexer_1_out : 8'bz;  // Controlled_Buffer controlled_buffer_1
  Multiplexer #(.width(8)) multiplexer_1 (
    .in0(bit_extender_2_out), .in1(register_1_q), .out(multiplexer_1_out), .sel(bit_extender_3_out));

  assign K_CLK = CLK;
endmodule
