// Logisim project Computer8Bit.circ as structural Verilog
module main (
);

  wire ADDR_SEL0, ADDR_SEL1, BASE_CLK, C1, C2, C3, C4, CSPC_UP, FLAGS_MODE_SEL0, FLAGS_MODE_SEL1,
       FLAGS_MODE_SEL2, J, JA, JC, JN, JZ, keyboard_1_avail, keyboardadapter_1_k_clear,
       keyboardadapter_1_k_clk, keyboardadapter_1_k_read_en, nor_1_out, nor_2_out, nor_3_out, nor_4_out,
       nor_5_out, nor_6_out, nor_7_out, not_1_out, not_2_out, NOT_ABH_IN, NOT_ABL_IN, NOT_CS_IN, NOT_CS_OUT,
       NOT_DATA_LATCH_OUT, NOT_DEVICE_IN, NOT_DEVICE_OE, NOT_DEVICE_OUT, NOT_DEVICE_SEL_0, NOT_DEVICE_SEL_1,
       NOT_DEVICE_SEL_2, NOT_DEVICE_SEL_3, NOT_DEVICE_SEL_4, NOT_DEVICE_SEL_5, NOT_DEVICE_SEL_RAM,
       NOT_DEVICE_SEL_ROM, NOT_DS_IN, NOT_DS_OUT, NOT_FETCH, NOT_FLAGS_OUT, NOT_HLT, NOT_IRQ, NOT_IVH_OUT,
       NOT_IVL_OUT, NOT_PASS, NOT_PC_IN, NOT_PC_INC, NOT_PC_OUT, NOT_RA_OUT, NOT_RB_IN, NOT_RB_OUT,
       NOT_RC_IN, NOT_RC_OUT, NOT_RD_IN, NOT_RD_OUT, NOT_RT_IN, NOT_RT_OUT, NOT_SP_OUT, NOT_SS_IN,
       NOT_SS_OUT, OP_SEL0, OP_SEL1, OP_SEL2, PHI1, PHI2, RA_S0, RA_S1, RESET, RESET_BTN_out, rgb_video_1_p1,
       rgb_video_1_p2, rgb_video_1_p3, rgb_video_1_p4, rgb_video_1_p5, rgb_video_1_p6, SP_MODE_SEL0,
       SP_MODE_SEL1, switch_1_p2, ttyadapter_1_tty_clr, ttyadapter_1_tty_we, X_SEL0, X_SEL1, X_SEL2, Y_SEL0,
       Y_SEL1, Y_SEL2;
  wire [2:0] alu_1_flags;
  wire [3:0] FLAGS_VAL, joystick_1_x, joystick_1_y;
  wire [6:0] keyboard_1_data, ttyadapter_1_tty_data;
  wire [7:0] ABH_q, ABL_q, aluoperandselector_1_o1, aluoperandselector_1_o2, aluoperatorselector_1_op_out,
       bufferedregister_1_async_out, controlunit_1_ir_out, DBUS, DL_VAL, DS_async_out, joystickadapter_1_p9,
       keyboardadapter_1_async_out, RA_VAL, RB_VAL, RC_VAL, RD_VAL, rgbscreenadapter_1_p7, RT_VAL, SP_VAL,
       SS_VAL, undriven;
  wire [15:0] ABUS, CS_PC;

  // Digital_Oscilloscope #(.frontlines("no"), .showclock("false")) digital_oscilloscope_1: pin names not known; wires that end beside it: BASE_CLK, PHI1, C1, C3
  // Probe on controlunit_1_ir_out
  // Probe on CS_PC
  // Probe on ABUS
  // Probe on DBUS
  // Probe on bufferedregister_1_async_out
  // Probe on RA_VAL
  // Probe on RB_VAL
  // Probe on RC_VAL
  // Probe on RD_VAL
  // Probe on RT_VAL
  // Probe on DL_VAL
  // Probe on SS_VAL
  // Probe on SP_VAL
  // Probe on FLAGS_VAL
  // DipSwitch dipswitch_1: pin names not known
  assign DBUS = switch_1_p2 ? undriven : 8'bz;  // Controlled_Buffer controlled_buffer_1
  // Switch switch_1: pin names not known; wires that end beside it: 1'b1, switch_1_p2
  Pull_Resistor pull_resistor_1 (.node(switch_1_p2));
  Hex_Digit_Display hex_digit_display_1 (.value(DBUS[7:4]));  // open: dp
  Hex_Digit_Display hex_digit_display_2 (.value(DBUS[3:0]));  // open: dp
  ControlUnit controlunit_1 (
    .IR_IN(bufferedregister_1_async_out), .NOT_IRQ(NOT_IRQ), .RESET(RESET), .CLK(C1), .I(FLAGS_VAL[3]),
    .IR_OUT(controlunit_1_ir_out), .RA_S0(RA_S0), .RA_S1(RA_S1), .NOT_RA_OUT(NOT_RA_OUT),
    .NOT_RB_IN(NOT_RB_IN), .NOT_RB_OUT(NOT_RB_OUT), .NOT_RC_IN(NOT_RC_IN), .NOT_RC_OUT(NOT_RC_OUT),
    .NOT_RD_IN(NOT_RD_IN), .NOT_RD_OUT(NOT_RD_OUT), .NOT_DEVICE_IN(NOT_DEVICE_IN),
    .NOT_DEVICE_OUT(NOT_DEVICE_OUT), .NOT_SS_IN(NOT_SS_IN), .NOT_SS_OUT(NOT_SS_OUT),
    .SP_MODE_SEL0(SP_MODE_SEL0), .SP_MODE_SEL1(SP_MODE_SEL1), .NOT_SP_OUT(NOT_SP_OUT),
    .NOT_ABH_IN(NOT_ABH_IN), .NOT_ABL_IN(NOT_ABL_IN), .NOT_RT_IN(NOT_RT_IN), .NOT_RT_OUT(NOT_RT_OUT),
    .X_SEL0(X_SEL0), .X_SEL1(X_SEL1), .X_SEL2(X_SEL2), .Y_SEL0(Y_SEL0), .Y_SEL1(Y_SEL1), .Y_SEL2(Y_SEL2),
    .OP_SEL0(OP_SEL0), .OP_SEL1(OP_SEL1), .OP_SEL2(OP_SEL2), .NOT_CS_IN(NOT_CS_IN), .NOT_PC_IN(NOT_PC_IN),
    .NOT_PC_INC(NOT_PC_INC), .NOT_CS_OUT(NOT_CS_OUT), .NOT_PC_OUT(NOT_PC_OUT), .J(J), .JC(JC), .JZ(JZ),
    .JN(JN), .JA(JA), .NOT_PASS(NOT_PASS), .NOT_HLT(NOT_HLT), .ADDR_SEL0(ADDR_SEL0), .ADDR_SEL1(ADDR_SEL1),
    .NOT_FETCH(NOT_FETCH), .NOT_DATA_LATCH_OUT(NOT_DATA_LATCH_OUT), .NOT_IVH_OUT(NOT_IVH_OUT),
    .NOT_IVL_OUT(NOT_IVL_OUT), .FLAGS_MODE_SEL0(FLAGS_MODE_SEL0), .FLAGS_MODE_SEL1(FLAGS_MODE_SEL1),
    .FLAGS_MODE_SEL2(FLAGS_MODE_SEL2), .NOT_FLAGS_OUT(NOT_FLAGS_OUT), .CSPC_UP(CSPC_UP),
    .NOT_DS_IN(NOT_DS_IN), .NOT_DS_OUT(NOT_DS_OUT));
  LED led_1 (.in(RA_S0));
  LED led_2 (.in(RA_S1));
  LED led_3 (.in(NOT_RA_OUT));
  LED led_4 (.in(NOT_RB_IN));
  LED led_5 (.in(NOT_RB_OUT));
  LED led_6 (.in(NOT_RC_IN));
  LED led_7 (.in(NOT_RC_OUT));
  LED led_8 (.in(NOT_RD_IN));
  LED led_9 (.in(NOT_RD_OUT));
  LED led_10 (.in(NOT_DEVICE_IN));
  LED led_11 (.in(NOT_DEVICE_OUT));
  LED led_12 (.in(NOT_SS_IN));
  LED led_13 (.in(NOT_SS_OUT));
  LED led_14 (.in(SP_MODE_SEL0));
  LED led_15 (.in(SP_MODE_SEL1));
  LED led_16 (.in(NOT_SP_OUT));
  LED led_17 (.in(NOT_ABH_IN));
  LED led_18 (.in(NOT_ABL_IN));
  LED led_19 (.in(NOT_RT_IN));
  LED led_20 (.in(NOT_RT_OUT));
  LED led_21 (.in(X_SEL0));
  LED led_22 (.in(X_SEL1));
  LED led_23 (.in(X_SEL2));
  LED led_24 (.in(Y_SEL0));
  LED led_25 (.in(Y_SEL1));
  LED led_26 (.in(Y_SEL2));
  LED led_27 (.in(OP_SEL0));
  LED led_28 (.in(OP_SEL1));
  LED led_29 (.in(OP_SEL2));
  LED led_30 (.in(NOT_CS_IN));
  LED led_31 (.in(NOT_PC_IN));
  LED led_32 (.in(NOT_PC_INC));
  LED led_33 (.in(NOT_CS_OUT));
  LED led_34 (.in(NOT_PC_OUT));
  LED led_35 (.in(J));
  LED led_36 (.in(JC));
  LED led_37 (.in(JZ));
  LED led_38 (.in(JN));
  LED led_39 (.in(JA));
  LED led_40 (.in(NOT_PASS));
  LED led_41 (.in(NOT_HLT));
  LED led_42 (.in(ADDR_SEL0));
  LED led_43 (.in(ADDR_SEL1));
  LED led_44 (.in(NOT_FETCH));
  LED led_45 (.in(NOT_DATA_LATCH_OUT));
  LED led_46 (.in(NOT_IVH_OUT));
  LED led_47 (.in(NOT_IVL_OUT));
  LED led_48 (.in(FLAGS_MODE_SEL0));
  LED led_49 (.in(FLAGS_MODE_SEL1));
  LED led_50 (.in(FLAGS_MODE_SEL2));
  LED led_51 (.in(NOT_FLAGS_OUT));
  LED led_52 (.in(CSPC_UP));
  Pull_Resistor #(.pull(1)) pull_resistor_2 (.node(NOT_IRQ));
  nor nor_1 (nor_1_out, NOT_DEVICE_SEL_0, NOT_DEVICE_OE);
  Keyboard keyboard_1 (
    .clk(keyboardadapter_1_k_clk), .re(keyboardadapter_1_k_read_en), .clr(keyboardadapter_1_k_clear),
    .avail(keyboard_1_avail), .data(keyboard_1_data));
  Hex_Digit_Display hex_digit_display_3 (.value(ABUS[11:8]));  // open: dp
  Hex_Digit_Display hex_digit_display_4 (.value(ABUS[15:12]));  // open: dp
  Button RESET_BTN (.out(RESET_BTN_out));
  Hex_Digit_Display hex_digit_display_5 (.value(ABUS[7:4]));  // open: dp
  Hex_Digit_Display hex_digit_display_6 (.value(ABUS[3:0]));  // open: dp
  Register ABH (.D(DBUS), .en(not_1_out), .clk(C4), .Q(ABH_q));  // open: clr
  not not_1 (not_1_out, NOT_ABH_IN);
  KeyboardAdapter keyboardadapter_1 (
    .K_AVAIL(keyboard_1_avail), .K_DATA(keyboard_1_data), .BUS_IN(DBUS), .ABUS(ABUS),
    .NOT_DEVICE_IN(NOT_DEVICE_IN), .NOT_DEVICE_OE(NOT_DEVICE_OE), .NOT_DEVICE_SEL(NOT_DEVICE_SEL_0),
    .CLK(C4), .NOT_IRQ(NOT_IRQ), .ASYNC_OUT(keyboardadapter_1_async_out),
    .K_READ_EN(keyboardadapter_1_k_read_en), .K_CLEAR(keyboardadapter_1_k_clear),
    .K_CLK(keyboardadapter_1_k_clk));
  Register ABL (.D(DBUS), .en(not_2_out), .clk(C4), .Q(ABL_q));  // open: clr
  not not_2 (not_2_out, NOT_ABL_IN);
  assign DBUS = nor_1_out ? keyboardadapter_1_async_out : 8'bz;  // Controlled_Buffer controlled_buffer_2
  ResetCircuit resetcircuit_1 (.RESET_BTN(RESET_BTN_out), .PHASE(PHI1), .RESET_OUT(RESET));
  DeviceOEPhaseSelector deviceoephaseselector_1 (
    .NOT_DEVICE_OUT(NOT_DEVICE_OUT), .NOT_FETCH(NOT_FETCH), .PHI1(PHI1), .PHI2(PHI2),
    .NOT_DEVICE_OE(NOT_DEVICE_OE));
  BufferedRegister DS (
    .BUS_IN(DBUS), .CLK(C4), .NOT_R_IN(NOT_DS_IN), .NOT_R_OUT(NOT_DS_OUT), .NOT_ENABLE(PHI1),
    .ASYNC_OUT(DS_async_out), .BUS_OUT(DBUS));  // open: RESET
  TTY #(.cols(56)) tty_1 (.data(ttyadapter_1_tty_data), .clk(C3), .we(ttyadapter_1_tty_we), .clr(ttyadapter_1_tty_clr));
  AddressSelector addressselector_1 (
    .ABL_in(ABL_q), .ABH_in(ABH_q), .DS_IN(DS_async_out), .SS_SP_in({SS_VAL, SP_VAL}), .CS_PC_in(CS_PC),
    .ADDR_SEL0(ADDR_SEL0), .ADDR_SEL1(ADDR_SEL1), .CSPC_override(PHI1), .ADDR_OUT(ABUS));
  nor nor_2 (nor_2_out, NOT_DEVICE_SEL_1, NOT_DEVICE_OE);
  AddrDecoder addrdecoder_1 (
    .ABUS(ABUS), .NOT_DEVICE_SEL_ROM(NOT_DEVICE_SEL_ROM), .NOT_DEVICE_SEL_RAM(NOT_DEVICE_SEL_RAM),
    .NOT_DEVICE_SEL_0(NOT_DEVICE_SEL_0), .NOT_DEVICE_SEL_1(NOT_DEVICE_SEL_1),
    .NOT_DEVICE_SEL_2(NOT_DEVICE_SEL_2), .NOT_DEVICE_SEL_3(NOT_DEVICE_SEL_3),
    .NOT_DEVICE_SEL_4(NOT_DEVICE_SEL_4), .NOT_DEVICE_SEL_5(NOT_DEVICE_SEL_5));
  BufferedRegister SS (
    .BUS_IN(DBUS), .CLK(C3), .NOT_R_IN(NOT_SS_IN), .NOT_R_OUT(NOT_SS_OUT), .NOT_ENABLE(PHI1),
    .ASYNC_OUT(SS_VAL), .BUS_OUT(DBUS));  // open: RESET
  StackPointer SP (
    .SP_MODE_SEL0(SP_MODE_SEL0), .SP_MODE_SEL1(SP_MODE_SEL1), .NOT_OUT(NOT_SP_OUT), .NOT_OE(PHI1), .CLK(C3),
    .DBUS(DBUS), .ASYNC_OUT(SP_VAL), .BUS_OUT(DBUS));
  CodeSegment_ProgramCounter CSPC (
    .FLAGS(FLAGS_VAL), .J(J), .JC(JC), .JZ(JZ), .JN(JN), .JA(JA), .NOT_PC_IN(NOT_PC_IN),
    .NOT_CS_IN(NOT_CS_IN), .NOT_PC_INC(NOT_PC_INC), .RESET(RESET), .ABUS(ABUS), .CLK(C3), .CSPC_UP(CSPC_UP),
    .NOT_PC_OUT(NOT_PC_OUT), .NOT_CS_OUT(NOT_CS_OUT), .NOT_OE(PHI1), .CS_PC(CS_PC), .BUS_OUT(DBUS));
  TTYAdapter ttyadapter_1 (
    .DBUS_IN(DBUS), .ABUS(ABUS), .NOT_DEVICE_IN(NOT_DEVICE_IN), .NOT_DEVICE_OE(NOT_DEVICE_OE),
    .NOT_DEVICE_SEL(NOT_DEVICE_SEL_1), .CLK(C3), .TTY_DATA(ttyadapter_1_tty_data),
    .TTY_WE(ttyadapter_1_tty_we), .TTY_CLR(ttyadapter_1_tty_clr));
  Controlled_Buffer #(.width(8)) controlled_buffer_3 (.out(DBUS), .en(nor_2_out));  // open: in
  TwoPhaseClock twophaseclock_1 (
    .NOT_HLT(NOT_HLT), .BASE_CLK(BASE_CLK), .PHI1(PHI1), .PHI2(PHI2), .C1(C1), .C2(C2), .C3(C3), .C4(C4));
  RAMModule RAM (
    .ABUS(ABUS), .CLK(C4), .BUS_IN(DBUS), .NOT_DEVICE_IN(NOT_DEVICE_IN),
    .NOT_DEVICE_SEL_RAM(NOT_DEVICE_SEL_RAM), .NOT_RAM_OE(NOT_DEVICE_OE), .DBUS_OUT(DBUS));
  ROMModule ROM (.ABUS(ABUS), .NOT_DEVICE_SEL_ROM(NOT_DEVICE_SEL_ROM), .NOT_ROM_OE(NOT_DEVICE_OE), .DBUS(DBUS));
  BufferedRegister bufferedregister_1 (
    .BUS_IN(DBUS), .CLK(C2), .NOT_R_IN(NOT_FETCH), .NOT_R_OUT(NOT_DATA_LATCH_OUT), .NOT_ENABLE(PHI1),
    .RESET(RESET), .ASYNC_OUT(bufferedregister_1_async_out), .BUS_OUT(DBUS));
  BufferedRegister bufferedregister_2 (
    .BUS_IN(DBUS), .CLK(C4), .NOT_R_IN(NOT_RT_IN), .NOT_R_OUT(NOT_RT_OUT), .NOT_ENABLE(PHI1), .RESET(RESET),
    .ASYNC_OUT(RT_VAL), .BUS_OUT(DBUS));
  nor nor_3 (nor_3_out, NOT_DEVICE_SEL_2, NOT_DEVICE_OE);
  // RGB_Video #(.cursor("No Cursor"), .height(32), .reset("Synchronous"), .scale(8), .width(64)) rgb_video_1: pin names not known; wires that end beside it: rgb_video_1_p1, rgb_video_1_p2, rgb_video_1_p3, rgb_video_1_p4, rgb_video_1_p5, rgb_video_1_p6
  nor nor_4 (nor_4_out, PHI1, NOT_IVL_OUT);
  assign DBUS = nor_4_out ? {8{1'b0}} : 8'bz;  // Controlled_Buffer controlled_buffer_4
  assign DBUS = nor_5_out ? 8'h1f : 8'bz;  // Controlled_Buffer controlled_buffer_5
  nor nor_5 (nor_5_out, PHI1, NOT_IVH_OUT);
  // RGBScreenAdapter rgbscreenadapter_1: pin names not known; wires that end beside it: DBUS, ABUS, NOT_DEVICE_IN, NOT_DEVICE_OE, NOT_DEVICE_SEL_2, C3, rgbscreenadapter_1_p7, rgb_video_1_p1, rgb_video_1_p2, rgb_video_1_p3, rgb_video_1_p4, rgb_video_1_p5, rgb_video_1_p6
  assign DBUS = nor_3_out ? rgbscreenadapter_1_p7 : 8'bz;  // Controlled_Buffer controlled_buffer_6
  BufferedRegister RC (
    .BUS_IN(DBUS), .CLK(C4), .NOT_R_IN(NOT_RC_IN), .NOT_R_OUT(NOT_RC_OUT), .NOT_ENABLE(PHI1),
    .ASYNC_OUT(RC_VAL), .BUS_OUT(DBUS));  // open: RESET
  Hex_Digit_Display hex_digit_display_7 (.value(RC_VAL[7:4]));  // open: dp
  ShiftRegister RA (
    .S0(RA_S0), .S1(RA_S1), .CLK(C4), .BUS_IN(DBUS), .NOT_OE(NOT_RA_OUT), .NOT_ENABLE(PHI1),
    .ASYNC_OUT(RA_VAL), .BUS_OUT(DBUS));
  Hex_Digit_Display hex_digit_display_8 (.value(RA_VAL[7:4]));  // open: dp
  Hex_Digit_Display hex_digit_display_9 (.value(RC_VAL[3:0]));  // open: dp
  Hex_Digit_Display hex_digit_display_10 (.value(RA_VAL[3:0]));  // open: dp
  ALUOperandSelector aluoperandselector_1 (
    .X_SEL0(X_SEL0), .X_SEL1(X_SEL1), .X_SEL2(X_SEL2), .Y_SEL0(Y_SEL0), .Y_SEL1(Y_SEL1), .Y_SEL2(Y_SEL2),
    .A_ASYNC(RA_VAL), .B_ASYNC(RB_VAL), .C_ASYNC(RC_VAL), .D_ASYNC(RD_VAL), .E_ASYNC(RT_VAL), .F_ASYNC(8'h1),
    .O1(aluoperandselector_1_o1), .O2(aluoperandselector_1_o2));
  Joystick joystick_1 (.x(joystick_1_x), .y(joystick_1_y));
  nor nor_6 (nor_6_out, NOT_DEVICE_SEL_3, NOT_DEVICE_OE);
  BufferedRegister RB (
    .BUS_IN(DBUS), .CLK(C4), .NOT_R_IN(NOT_RB_IN), .NOT_R_OUT(NOT_RB_OUT), .NOT_ENABLE(PHI1),
    .ASYNC_OUT(RB_VAL), .BUS_OUT(DBUS));  // open: RESET
  Hex_Digit_Display hex_digit_display_11 (.value(joystick_1_y));  // open: dp
  BufferedRegister RD (
    .BUS_IN(DBUS), .CLK(C4), .NOT_R_IN(NOT_RD_IN), .NOT_R_OUT(NOT_RD_OUT), .NOT_ENABLE(PHI1),
    .ASYNC_OUT(RD_VAL), .BUS_OUT(DBUS));  // open: RESET
  Hex_Digit_Display hex_digit_display_12 (.value(RD_VAL[7:4]));  // open: dp
  Hex_Digit_Display hex_digit_display_13 (.value(RD_VAL[3:0]));  // open: dp
  Hex_Digit_Display hex_digit_display_14 (.value(RB_VAL[7:4]));  // open: dp
  Hex_Digit_Display hex_digit_display_15 (.value(RB_VAL[3:0]));  // open: dp
  ALUOperatorSelector aluoperatorselector_1 (
    .OP_SEL0(OP_SEL0), .OP_SEL1(OP_SEL1), .OP_SEL2(OP_SEL2), .OP_OUT(aluoperatorselector_1_op_out));
  ALU alu_1 (
    .OPERATORS(aluoperatorselector_1_op_out), .O1(aluoperandselector_1_o1), .O2(aluoperandselector_1_o2),
    .NOT_ENABLE(PHI1), .BUS_OUT(DBUS), .FLAGS(alu_1_flags));
  FLAGSRegister FLAGS (
    .MODE2(FLAGS_MODE_SEL2), .MODE1(FLAGS_MODE_SEL1), .MODE0(FLAGS_MODE_SEL0), .BUS_IN(DBUS),
    .ALU_IN(alu_1_flags), .CLK(C4), .FLAGS_OUT(FLAGS_VAL));
  LED led_53 (.in(FLAGS_VAL[3]));
  LED led_54 (.in(FLAGS_VAL[2]));
  LED led_55 (.in(FLAGS_VAL[1]));
  // JoystickAdapter joystickadapter_1: pin names not known; wires that end beside it: DBUS, ABUS, NOT_DEVICE_IN, NOT_DEVICE_OE, NOT_DEVICE_SEL_3, C3, joystick_1_x, joystick_1_y, joystickadapter_1_p9, NOT_IRQ
  LED led_56 (.in(FLAGS_VAL[0]));
  nor nor_7 (nor_7_out, PHI1, NOT_FLAGS_OUT);
  assign DBUS = nor_7_out ? {4'b0000, FLAGS_VAL} : 8'bz;  // Controlled_Buffer controlled_buffer_7
  assign DBUS = nor_6_out ? joystickadapter_1_p9 : 8'bz;  // Controlled_Buffer controlled_buffer_8

  // Notes on the sheet:
  //   IR
  //   CS_PC
  //   ABUS
  //   DBUS
  //   DL
  //   RA
  //   RB
  //   RC
  //   RD
  //   RT
  //   DL
  //   SS
  //   SP
  //   INZC
  //   Click here with the poke tool to type into the serial port ->
  //   Write to bus
  //   Data bus
  //   Address bus
  //   Clock
  //   RAM
  //   ROM
  //   DATA LATCH
  //   RT
  //   RC
  //   RA
  //   ALU_OPERAND_SELECTOR
  //   RD
  //   RB
  //   ALU_OPERATOR_SELECTOR
  //   I
  //   N
  //   Z
  //   C
endmodule

module ShiftRegister (
  input  S0,
  input  S1,
  input  CLK,
  input  [7:0] BUS_IN,
  input  NOT_OE,
  input  NOT_ENABLE,
  output [7:0] ASYNC_OUT,
  output [7:0] BUS_OUT
);

  wire nor_1_out;

  nor nor_1 (nor_1_out, NOT_OE, NOT_ENABLE);
  L_4_bit_bidir_univ_shift_register_sn74194 l_4_bit_bidir_univ_shift_register_sn74194_1 (
    .SL_SERIAL(ASYNC_OUT[3]), .DATA_IN(BUS_IN[7:4]), .SR_SERIAL(1'b0), .CLK(CLK), .NOT_CLR(1'b1), .S0(S0),
    .S1(S1), .DATA_OUT(ASYNC_OUT[7:4]));
  L_4_bit_bidir_univ_shift_register_sn74194 l_4_bit_bidir_univ_shift_register_sn74194_2 (
    .SL_SERIAL(1'b0), .DATA_IN(BUS_IN[3:0]), .SR_SERIAL(ASYNC_OUT[4]), .CLK(CLK), .NOT_CLR(1'b1), .S0(S0),
    .S1(S1), .DATA_OUT(ASYNC_OUT[3:0]));
  assign BUS_OUT = nor_1_out ? ASYNC_OUT : 8'bz;  // Controlled_Buffer controlled_buffer_1
endmodule

module BufferedRegister (
  input  [7:0] BUS_IN,
  input  CLK,
  input  NOT_R_IN,
  input  NOT_R_OUT,
  input  NOT_ENABLE,
  input  RESET,
  output [7:0] ASYNC_OUT,
  output [7:0] BUS_OUT
);

  wire nor_1_out, not_1_out;

  Register register_1 (.D(BUS_IN), .en(not_1_out), .clk(CLK), .Q(ASYNC_OUT), .clr(RESET));
  not not_1 (not_1_out, NOT_R_IN);
  nor nor_1 (nor_1_out, NOT_R_OUT, NOT_ENABLE);
  assign BUS_OUT = nor_1_out ? ASYNC_OUT : 8'bz;  // Controlled_Buffer controlled_buffer_1
endmodule

module ALUOperandSelector (
  input  X_SEL0,
  input  X_SEL1,
  input  X_SEL2,
  input  Y_SEL0,
  input  Y_SEL1,
  input  Y_SEL2,
  input  [7:0] A_ASYNC,
  input  [7:0] B_ASYNC,
  input  [7:0] C_ASYNC,
  input  [7:0] D_ASYNC,
  input  [7:0] E_ASYNC,
  input  [7:0] F_ASYNC,
  output [7:0] O1,
  output [7:0] O2
);

  wire decoder_1_out0, decoder_1_out1, decoder_1_out2, decoder_1_out3, decoder_1_out4, decoder_1_out5,
       decoder_2_out0, decoder_2_out1, decoder_2_out2, decoder_2_out3, decoder_2_out4, decoder_2_out5;

  Decoder #(.select(3)) decoder_1 (
    .out0(decoder_1_out0), .out1(decoder_1_out1), .out2(decoder_1_out2), .out3(decoder_1_out3),
    .out4(decoder_1_out4), .out5(decoder_1_out5), .sel({X_SEL2, X_SEL1, X_SEL0}), .en(1'b1));  // open: out6, out7
  Decoder #(.select(3)) decoder_2 (
    .out0(decoder_2_out0), .out1(decoder_2_out1), .out2(decoder_2_out2), .out3(decoder_2_out3),
    .out4(decoder_2_out4), .out5(decoder_2_out5), .sel({Y_SEL2, Y_SEL1, Y_SEL0}), .en(1'b1));  // open: out6, out7
  assign O2 = decoder_2_out2 ? C_ASYNC : 8'bz;  // Controlled_Buffer controlled_buffer_1
  assign O2 = decoder_2_out3 ? D_ASYNC : 8'bz;  // Controlled_Buffer controlled_buffer_2
  assign O2 = decoder_2_out4 ? E_ASYNC : 8'bz;  // Controlled_Buffer controlled_buffer_3
  assign O2 = decoder_2_out5 ? F_ASYNC : 8'bz;  // Controlled_Buffer controlled_buffer_4
  assign O2 = decoder_2_out0 ? A_ASYNC : 8'bz;  // Controlled_Buffer controlled_buffer_5
  assign O2 = decoder_2_out1 ? B_ASYNC : 8'bz;  // Controlled_Buffer controlled_buffer_6
  assign O1 = decoder_1_out0 ? A_ASYNC : 8'bz;  // Controlled_Buffer controlled_buffer_7
  assign O1 = decoder_1_out1 ? B_ASYNC : 8'bz;  // Controlled_Buffer controlled_buffer_8
  assign O1 = decoder_1_out2 ? C_ASYNC : 8'bz;  // Controlled_Buffer controlled_buffer_9
  assign O1 = decoder_1_out3 ? D_ASYNC : 8'bz;  // Controlled_Buffer controlled_buffer_10
  assign O1 = decoder_1_out4 ? E_ASYNC : 8'bz;  // Controlled_Buffer controlled_buffer_11
  assign O1 = decoder_1_out5 ? F_ASYNC : 8'bz;  // Controlled_Buffer controlled_buffer_12
endmodule

module ALUOperatorSelector (
  input  OP_SEL0,
  input  OP_SEL1,
  input  OP_SEL2,
  output [7:0] OP_OUT
);

  Decoder #(.select(3)) decoder_1 (
    .out0(OP_OUT[0]), .out1(OP_OUT[1]), .out2(OP_OUT[2]), .out3(OP_OUT[3]), .out4(OP_OUT[4]),
    .out5(OP_OUT[5]), .out6(OP_OUT[6]), .out7(OP_OUT[7]), .sel({OP_SEL2, OP_SEL1, OP_SEL0}), .en(1'b1));
endmodule

module FLAGSRegister (
  input  MODE2,
  input  MODE1,
  input  MODE0,
  input  [7:0] BUS_IN,
  input  [2:0] ALU_IN,
  input  CLK,
  output [3:0] FLAGS_OUT
);

  wire flagscontroller_1_c_val, flagscontroller_1_i_val, flagscontroller_1_n_val, flagscontroller_1_not_c_in,
       flagscontroller_1_not_i_in, flagscontroller_1_not_n_in, flagscontroller_1_not_z_in,
       flagscontroller_1_z_val, not_1_out, not_2_out, not_3_out, not_4_out;
  wire [3:0] bit_extender_1_out;

  Bit_Extender #(.out_width(4)) bit_extender_1 (.in(BUS_IN), .out(bit_extender_1_out));
  FLAGSController flagscontroller_1 (
    .MODE2(MODE2), .MODE1(MODE1), .MODE0(MODE0), .BUS_IN(bit_extender_1_out), .ALU_IN(ALU_IN),
    .NOT_C_IN(flagscontroller_1_not_c_in), .NOT_Z_IN(flagscontroller_1_not_z_in),
    .NOT_N_IN(flagscontroller_1_not_n_in), .NOT_I_IN(flagscontroller_1_not_i_in),
    .C_VAL(flagscontroller_1_c_val), .Z_VAL(flagscontroller_1_z_val), .N_VAL(flagscontroller_1_n_val),
    .I_VAL(flagscontroller_1_i_val));
  Register #(.width(1)) C (.D(flagscontroller_1_c_val), .en(not_1_out), .clk(CLK), .Q(FLAGS_OUT[0]));  // open: clr
  not not_1 (not_1_out, flagscontroller_1_not_c_in);
  Register #(.width(1)) Z (.D(flagscontroller_1_z_val), .en(not_2_out), .clk(CLK), .Q(FLAGS_OUT[1]));  // open: clr
  not not_2 (not_2_out, flagscontroller_1_not_z_in);
  Register #(.width(1)) N (.D(flagscontroller_1_n_val), .en(not_3_out), .clk(CLK), .Q(FLAGS_OUT[2]));  // open: clr
  not not_3 (not_3_out, flagscontroller_1_not_n_in);
  Register #(.width(1)) I (.D(flagscontroller_1_i_val), .en(not_4_out), .clk(CLK), .Q(FLAGS_OUT[3]));  // open: clr
  not not_4 (not_4_out, flagscontroller_1_not_i_in);
endmodule

module ALU (
  input  [7:0] OPERATORS,
  input  [7:0] O1,
  input  [7:0] O2,
  input  NOT_ENABLE,
  output [7:0] BUS_OUT,
  output [2:0] FLAGS
);

  wire adder_1_cout, and_2_out, and_3_out, nor_1_out, nor_2_out, nor_3_out, nor_4_out, not_2_out, or_2_out;
  wire [6:0] buffer_1_out;
  wire [7:0] adder_1_out, and_1_out, bit_extender_1_out, controlled_buffer_1_out, not_1_out, or_1_out,
       xor_1_out, xor_2_out;

  assign not_1_out = ~O1;  // NOT_Gate not_1, 8 bits wide
  assign xor_1_out = O1 ^ O2;  // XOR_Gate xor_1, 8 bits wide
  assign controlled_buffer_1_out = OPERATORS[6] ? not_1_out : 8'bz;  // Controlled_Buffer controlled_buffer_1
  assign controlled_buffer_1_out = OPERATORS[5] ? xor_1_out : 8'bz;  // Controlled_Buffer controlled_buffer_2
  assign and_1_out = O1 & O2;  // AND_Gate and_1, 8 bits wide
  assign controlled_buffer_1_out = OPERATORS[4] ? and_1_out : 8'bz;  // Controlled_Buffer controlled_buffer_3
  not not_2 (not_2_out, NOT_ENABLE);
  // NoConnect on OPERATORS[7]
  assign or_1_out = O1 | O2;  // OR_Gate or_1, 8 bits wide
  assign controlled_buffer_1_out = OPERATORS[3] ? or_1_out : 8'bz;  // Controlled_Buffer controlled_buffer_4
  nor nor_1 (nor_1_out, FLAGS[2], buffer_1_out[6]);
  assign bit_extender_1_out = {{7{OPERATORS[2]}}, OPERATORS[2]};  // Bit_Extender bit_extender_1
  assign {FLAGS[2], buffer_1_out} = controlled_buffer_1_out;  // Buffer buffer_1, 8 bits wide
  Pull_Resistor pull_resistor_1 (.node({FLAGS[2], buffer_1_out}));
  nor nor_2 (nor_2_out, buffer_1_out[5], buffer_1_out[4]);
  nor nor_3 (nor_3_out, buffer_1_out[3], buffer_1_out[2]);
  and and_2 (and_2_out, nor_1_out, nor_2_out);
  and and_3 (and_3_out, nor_3_out, nor_4_out);
  and and_4 (FLAGS[1], and_2_out, and_3_out);
  Adder adder_1 (.a(O1), .b(xor_2_out), .out(adder_1_out), .cin(OPERATORS[2]), .cout(adder_1_cout));
  assign xor_2_out = O2 ^ bit_extender_1_out;  // XOR_Gate xor_2, 8 bits wide
  assign controlled_buffer_1_out = or_2_out ? adder_1_out : 8'bz;  // Controlled_Buffer controlled_buffer_5
  xor xor_3 (FLAGS[0], OPERATORS[2], adder_1_cout);
  nor nor_4 (nor_4_out, buffer_1_out[1], buffer_1_out[0]);
  or or_2 (or_2_out, OPERATORS[2], OPERATORS[1]);
  assign BUS_OUT = not_2_out ? controlled_buffer_1_out : 8'bz;  // Controlled_Buffer controlled_buffer_6

  // Notes on the sheet:
  //   we invert the carry when subtracting, so that the carry flag in a sub operation means "borrow"
endmodule

module ClockModule (
  input  NOT_HLT,
  output C1,
  output C3,
  output C2,
  output C4
);

  wire and_1_out, and_2_out, CLK_GEN_out, nor_1_out, nor_2_out, nor_3_out, nor_4_out, not_1_out, not_2_out,
       not_3_out, not_4_out, not_5_out, not_6_out, not_7_out, not_8_out, not_9_out, not_10_out, not_11_out,
       not_12_out, sysclk_out;

  Clock #(.highDuration(2), .lowDuration(2), .phaseOffset(3)) CLK_GEN (.out(CLK_GEN_out));
  Clock #(.highDuration(2), .lowDuration(2), .phaseOffset(1)) sysclk (.out(sysclk_out));
  and and_1 (and_1_out, CLK_GEN_out, NOT_HLT);
  and and_2 (and_2_out, NOT_HLT, sysclk_out);
  nor nor_1 (nor_1_out, ~and_1_out, C3);  // NOR_Gate
  nor nor_2 (nor_2_out, C1, and_1_out);
  nor nor_3 (nor_3_out, ~and_2_out, C4);  // NOR_Gate
  nor nor_4 (nor_4_out, C2, and_2_out);
  not not_1 (not_1_out, nor_1_out);
  not not_2 (not_2_out, not_1_out);
  not not_3 (not_3_out, not_2_out);
  not not_4 (not_4_out, nor_2_out);
  not not_5 (not_5_out, not_4_out);
  not not_6 (not_6_out, not_5_out);
  not not_7 (not_7_out, nor_3_out);
  not not_8 (not_8_out, not_7_out);
  not not_9 (not_9_out, not_8_out);
  not not_10 (not_10_out, nor_4_out);
  not not_11 (not_11_out, not_10_out);
  not not_12 (not_12_out, not_11_out);
  not not_13 (C1, not_3_out);
  not not_14 (C3, not_6_out);
  not not_15 (C2, not_9_out);
  not not_16 (C4, not_12_out);
endmodule

module InstructionRegister (
);

  Counter counter_1 ();  // open: clr, load, up, count, clk, D, carry, Q
endmodule

module RAMModule (
  input  [15:0] ABUS,
  input  CLK,
  input  [7:0] BUS_IN,
  input  NOT_DEVICE_IN,
  input  NOT_DEVICE_SEL_RAM,
  input  NOT_RAM_OE,
  output [7:0] DBUS_OUT
);

  wire nor_1_out, not_1_out, or_1_out;
  wire [7:0] ram_1_dout;
  wire [12:0] bit_extender_1_out;

  Bit_Extender #(.in_width(16), .out_width(13), .\type ("zero")) bit_extender_1 (.in(ABUS), .out(bit_extender_1_out));
  or or_1 (or_1_out, NOT_DEVICE_IN, NOT_DEVICE_SEL_RAM);
  RAM #(.addrWidth(13), .asyncread("true")) ram_1 (
    .addr(bit_extender_1_out), .we(not_1_out), .oe(1'b1), .clk(CLK), .din(BUS_IN), .dout(ram_1_dout));
  not not_1 (not_1_out, or_1_out);
  assign DBUS_OUT = nor_1_out ? ram_1_dout : 8'bz;  // Controlled_Buffer controlled_buffer_1
  nor nor_1 (nor_1_out, NOT_DEVICE_SEL_RAM, NOT_RAM_OE);
endmodule

module StackPointer (
  input  SP_MODE_SEL0,
  input  SP_MODE_SEL1,
  input  NOT_OUT,
  input  NOT_OE,
  input  CLK,
  input  [7:0] DBUS,
  output [7:0] ASYNC_OUT,
  output [7:0] BUS_OUT
);

  wire and_1_out, nor_1_out, or_1_out;

  or or_1 (or_1_out, SP_MODE_SEL0, SP_MODE_SEL1);
  and and_1 (and_1_out, SP_MODE_SEL1, SP_MODE_SEL0);
  Counter counter_1 (
    .load(and_1_out), .up(SP_MODE_SEL0), .count(or_1_out), .clk(CLK), .D(DBUS), .Q(ASYNC_OUT));  // open: clr, carry
  nor nor_1 (nor_1_out, NOT_OUT, NOT_OE);
  assign BUS_OUT = nor_1_out ? ASYNC_OUT : 8'bz;  // Controlled_Buffer controlled_buffer_1

  // Notes on the sheet:
  //   SP_MODE_SEL
  //   00 - inactive
  //   01 - count up
  //   10 - count down
  //   11 - load
endmodule

module ROMModule (
  input  [15:0] ABUS,
  input  NOT_DEVICE_SEL_ROM,
  input  NOT_ROM_OE,
  output [7:0] DBUS
);

  wire nor_1_out;
  wire [7:0] STORAGE_ROM_data;
  wire [12:0] bit_extender_1_out;

  Bit_Extender #(.in_width(16), .out_width(13), .\type ("zero")) bit_extender_1 (.in(ABUS), .out(bit_extender_1_out));
  ROM #(.addrWidth(13)) STORAGE_ROM (.addr(bit_extender_1_out), .data(STORAGE_ROM_data));
  assign DBUS = nor_1_out ? STORAGE_ROM_data : 8'bz;  // Controlled_Buffer controlled_buffer_1
  nor nor_1 (nor_1_out, NOT_DEVICE_SEL_ROM, NOT_ROM_OE);

  // Notes on the sheet:
  //   contents of STORAGE_ROM (hex, n*v repeats v):
  //   9 21 8 0 a 20 f8 0 31 6 80 7 0 f8 0 9f 4 ff f8 0 42 6 80 7 0 4 8a 5 a f8 0 a4 4 66 f8 0 42 6 83 7 12
  //   4 96 5 22 f8 0 a4 1 25 0 0 fa 3b 3c 6 22 24 0 e5 2a 20 0 44 43 fa 3b 3c 6 22 24 0 26 e0 20 0 44 43
  //   fa 3b 3c 6 22 24 0 e5 2b 20 0 44 43 fa 3b 3c 6 22 24 0 27 e0 20 0 44 43 fa 3c 6 22 24 0 e5 2c 20 0
  //   44 fa 3a 3b 3c 15 6 22 24 0 27 e0 20 0 44 43 42 fa 3b 6 22 24 0 e5 20 0 2d 43 fa 3a 3b 3c 18 6 22 24
  //   0 27 e0 20 0 44 43 42 fa 37 9f ff ff fa 39 3a 3b 3c 39 3b 3a 3a 39 39 f8 0 35 f8 0 c8 42 f8 0 d4 43
  //   42 f8 0 c8 44 43 42 f8 0 d4 44 43 42 41 fa 3a 3c 26 e0 7f ef d1 f2 ca 44 42 fa 3a 3b 26 df 7e ef dd
  //   f2 d6 43 42 fa
endmodule

module CodeSegment_ProgramCounter (
  input  [3:0] FLAGS,
  input  J,
  input  JC,
  input  JZ,
  input  JN,
  input  JA,
  input  NOT_PC_IN,
  input  NOT_CS_IN,
  input  NOT_PC_INC,
  input  RESET,
  input  [15:0] ABUS,
  input  CLK,
  input  CSPC_UP,
  input  NOT_PC_OUT,
  input  NOT_CS_OUT,
  input  NOT_OE,
  output [15:0] CS_PC,
  output [7:0] BUS_OUT
);

  wire and_1_out, and_2_out, and_3_out, and_4_out, and_5_out, nor_1_out, nor_2_out, nor_3_out, not_1_out,
       not_2_out, not_3_out, or_1_out, or_2_out, or_3_out, or_4_out, or_5_out, PC_carry;

  and and_1 (and_1_out, JC, FLAGS[0]);
  or or_1 (or_1_out, and_1_out, and_2_out);
  and and_2 (and_2_out, JZ, FLAGS[1]);
  and and_3 (and_3_out, JN, FLAGS[2]);
  or or_2 (or_2_out, and_3_out, and_4_out);
  or or_3 (or_3_out, or_1_out, or_2_out);
  nor nor_1 (nor_1_out, J, or_3_out);
  and and_4 (and_4_out, JA, FLAGS[3]);
  nor nor_2 (nor_2_out, NOT_CS_IN, nor_1_out);
  and and_5 (and_5_out, CLK, RESET);
  Counter CS (
    .clr(and_5_out), .load(nor_2_out), .up(CSPC_UP), .count(PC_carry), .clk(CLK), .D(ABUS[15:8]),
    .Q(CS_PC[15:8]));  // open: carry
  not not_1 (not_1_out, NOT_PC_INC);
  nor nor_3 (nor_3_out, nor_1_out, NOT_PC_IN);
  Counter PC (
    .clr(and_5_out), .load(nor_3_out), .up(CSPC_UP), .count(not_1_out), .clk(CLK), .D(ABUS[7:0]),
    .carry(PC_carry), .Q(CS_PC[7:0]));
  assign BUS_OUT = not_3_out ? CS_PC[15:8] : 8'bz;  // Controlled_Buffer controlled_buffer_1
  assign BUS_OUT = not_2_out ? CS_PC[7:0] : 8'bz;  // Controlled_Buffer controlled_buffer_2
  not not_2 (not_2_out, or_4_out);
  not not_3 (not_3_out, or_5_out);
  or or_4 (or_4_out, NOT_OE, NOT_PC_OUT);
  or or_5 (or_5_out, NOT_OE, NOT_CS_OUT);
endmodule

module LCD_emulator (
  input  RS,
  input  R_NW,
  input  LCD_EN,
  input  [7:0] BUS_IN
);
endmodule

module Interface_emulator (
  input  POLL,
  input  TRANSMIT,
  input  CLK,
  input  [7:0] BUS_IN,
  output [7:0] BUS_OUT,
  output A_OUT
);

  wire [7:0] register_1_q;

  Register register_1 (.D(BUS_IN), .en(TRANSMIT), .clk(CLK), .Q(register_1_q));  // open: clr
  assign BUS_OUT = POLL ? register_1_q : 8'bz;  // Controlled_Buffer controlled_buffer_1

  assign A_OUT = POLL;
endmodule

module ControlUnit (
  input  [7:0] IR_IN,
  input  NOT_IRQ,
  input  RESET,
  input  CLK,
  input  I,
  output [7:0] IR_OUT,
  output RA_S0,
  output RA_S1,
  output NOT_RA_OUT,
  output NOT_RB_IN,
  output NOT_RB_OUT,
  output NOT_RC_IN,
  output NOT_RC_OUT,
  output NOT_RD_IN,
  output NOT_RD_OUT,
  output NOT_DEVICE_IN,
  output NOT_DEVICE_OUT,
  output NOT_SS_IN,
  output NOT_SS_OUT,
  output SP_MODE_SEL0,
  output SP_MODE_SEL1,
  output NOT_SP_OUT,
  output NOT_ABH_IN,
  output NOT_ABL_IN,
  output NOT_RT_IN,
  output NOT_RT_OUT,
  output X_SEL0,
  output X_SEL1,
  output X_SEL2,
  output Y_SEL0,
  output Y_SEL1,
  output Y_SEL2,
  output OP_SEL0,
  output OP_SEL1,
  output OP_SEL2,
  output NOT_CS_IN,
  output NOT_PC_IN,
  output NOT_PC_INC,
  output NOT_CS_OUT,
  output NOT_PC_OUT,
  output J,
  output JC,
  output JZ,
  output JN,
  output JA,
  output NOT_PASS,
  output NOT_HLT,
  output ADDR_SEL0,
  output ADDR_SEL1,
  output NOT_FETCH,
  output NOT_DATA_LATCH_OUT,
  output NOT_IVH_OUT,
  output NOT_IVL_OUT,
  output FLAGS_MODE_SEL0,
  output FLAGS_MODE_SEL1,
  output FLAGS_MODE_SEL2,
  output NOT_FLAGS_OUT,
  output CSPC_UP,
  output NOT_DS_IN,
  output NOT_DS_OUT
);

  wire and_1_out, n74163_1_pin3, n74163_1_pin10, not_1_out, not_2_out, or_1_out;
  wire [3:0] n74163_1_pin14;
  wire [7:0] multiplexer_1_out;
  wire [7:6] EEPROM6_data;

  Multiplexer #(.width(8)) multiplexer_1 (.in0(8'h2), .in1(IR_IN), .out(multiplexer_1_out), .sel(or_1_out));
  or or_1 (or_1_out, NOT_IRQ, I);
  not not_1 (not_1_out, RESET);
  Register IR (.D(multiplexer_1_out), .en(not_2_out), .clk(CLK), .Q(IR_OUT), .clr(RESET));
  not not_2 (not_2_out, NOT_PASS);
  and and_1 (and_1_out, NOT_PASS, not_1_out);
  _74163 u_74163_1 (
    .pin1(and_1_out), .pin2(CLK), .pin3(n74163_1_pin3), .pin4(n74163_1_pin3), .pin5(n74163_1_pin3),
    .pin6(n74163_1_pin3), .pin7(n74163_1_pin3), .pin14(n74163_1_pin14[0]), .pin13(n74163_1_pin14[1]),
    .pin12(n74163_1_pin14[2]), .pin11(n74163_1_pin14[3]), .pin10(n74163_1_pin10), .pin9(n74163_1_pin10));  // open: pin15
  ROM #(.addrWidth(13)) EEPROM0 (
    .addr({1'b0, IR_OUT, n74163_1_pin14}),
    .data({NOT_RD_IN, NOT_RC_OUT, NOT_RC_IN, NOT_RB_OUT, NOT_RB_IN, NOT_RA_OUT, RA_S1, RA_S0}));
  ROM #(.addrWidth(13)) EEPROM1 (
    .addr({1'b0, IR_OUT, n74163_1_pin14}),
    .data({NOT_SP_OUT, SP_MODE_SEL1, SP_MODE_SEL0, NOT_SS_OUT, NOT_SS_IN, NOT_DEVICE_OUT, NOT_DEVICE_IN, NOT_RD_OUT}));
  ROM #(.addrWidth(13)) EEPROM2 (
    .addr({1'b0, IR_OUT, n74163_1_pin14}),
    .data({Y_SEL0, X_SEL2, X_SEL1, X_SEL0, NOT_RT_OUT, NOT_RT_IN, NOT_ABL_IN, NOT_ABH_IN}));
  ROM #(.addrWidth(13)) EEPROM3 (
    .addr({1'b0, IR_OUT, n74163_1_pin14}),
    .data({NOT_PC_INC, NOT_PC_IN, NOT_CS_IN, OP_SEL2, OP_SEL1, OP_SEL0, Y_SEL2, Y_SEL1}));
  ROM #(.addrWidth(13)) EEPROM4 (
    .addr({1'b0, IR_OUT, n74163_1_pin14}), .data({NOT_PASS, JA, JN, JZ, JC, J, NOT_PC_OUT, NOT_CS_OUT}));
  ROM #(.addrWidth(13)) EEPROM5 (
    .addr({1'b0, IR_OUT, n74163_1_pin14}),
    .data({FLAGS_MODE_SEL0, NOT_IVL_OUT, NOT_IVH_OUT, NOT_DATA_LATCH_OUT, NOT_FETCH, ADDR_SEL1, ADDR_SEL0, NOT_HLT}));
  ROM #(.addrWidth(13)) EEPROM6 (
    .addr({1'b0, IR_OUT, n74163_1_pin14}),
    .data({EEPROM6_data, NOT_DS_OUT, NOT_DS_IN, CSPC_UP, NOT_FLAGS_OUT, FLAGS_MODE_SEL2, FLAGS_MODE_SEL1}));
  // also tied to VCC on the sheet: {n74163_1_pin3, n74163_1_pin10}

  // Notes on the sheet:
  //   Get the 163! Synchronous reset
  //   contents of EEPROM0 (hex, n*v repeats v):
  //   64*fc ff 15*fc f4 15*fc dc 15*fc 7c 63*fc 7c 15*fc 7c 15*fc 7c 15*fc f0 15*fc d8 15*fc 78 15*fc ef
  //   15*fc cc 15*fc 6c 15*fc bf 15*fc b4 15*fc 3c 15*fc ff 15*fc f4 15*fc dc 64*fc f8 15*fc ec 15*fc bc
  //   31*fc ff 15*fc f4 15*fc dc 15*fc 7c 30*fc bc fc f8 13*fc bc fc ec 13*fc bc fc bc 13*fc bc 15*fc bc
  //   fc ff 13*fc bc fc f4 13*fc bc fc dc 13*fc bc fc 7c 13*fc bc 17*fc f8 15*fc ec 15*fc bc 31*fc ff
  //   15*fc f4 15*fc dc 15*fc 7c 45*fc f8 15*fc ec 15*fc bc 47*fc bc 47*fc ff 15*fc f4 15*fc dc 15*fc 7c
  //   32*fc bc 30*fc ff 15*fc ff 15*fc ff 15*fc ff 15*fc f4 15*fc f4 15*fc f4 15*fc f4 15*fc dc 15*fc dc
  //   15*fc dc 15*fc dc 15*fc 7c 15*fc 7c 15*fc 7c 15*fc 7c 16*fc ff 15*fc f4 15*fc dc 15*fc 7c 78*fc ff
  //   15*fc ff 15*fc ff 15*fc ff 15*fc f4 15*fc f4 15*fc f4 15*fc f4 15*fc dc 15*fc dc 15*fc dc 15*fc dc
  //   15*fc 7c 15*fc 7c 15*fc 7c 15*fc 7c 16*fc ff 15*fc f4 15*fc dc 15*fc 7c 462*fc ff 15*fc ff 15*fc ff
  //   15*fc ff 15*fc f4 15*fc f4 15*fc f4 15*fc f4 15*fc dc 15*fc dc 15*fc dc 15*fc dc 15*fc 7c 15*fc 7c
  //   15*fc 7c 15*fc 7c 16*fc ff 15*fc f4 15*fc dc 15*fc 7c 78*fc ff 15*fc ff 15*fc ff 15*fc ff 15*fc f4
  //   15*fc f4 15*fc f4 15*fc f4 15*fc dc 15*fc dc 15*fc dc 15*fc dc 15*fc 7c 15*fc 7c 15*fc 7c 15*fc 7c
  //   16*fc ff 15*fc f4 15*fc dc 15*fc 7c 78*fc ff 15*fc ff 15*fc ff 15*fc ff 15*fc f4 15*fc f4 15*fc f4
  //   15*fc f4 15*fc dc 15*fc dc 15*fc dc 15*fc dc 15*fc 7c 15*fc 7c 15*fc 7c 15*fc 7c 16*fc ff 15*fc f4
  //   15*fc dc 15*fc 7c 78*fc ff 15*fc f4 15*fc dc 15*fc 7c 31*fc ff 15*fc f4 15*fc dc 15*fc 7c 31*fc ff
  //   15*fc f4 15*fc dc 15*fc 7c 31*fc fe 15*fc fd 15*fc f8 ef f4 13*fc f8 bf dc 13*fc f8 ff 7c 13*fc ec
  //   b4 dc 13*fc ec f4 7c 13*fc bc dc 7c 141*fc bc 31*fc bc 4207*fc
  //   contents of EEPROM1 (hex, n*v repeats v):
  //   34*9f 9d bd bd bf 12*9f 9d bd bd bf 74*9f ff 15*9f 97 31*9f 8f 15*9f 1f 175*9f 9e 15*9f 9e 15*9f 9e
  //   15*9f 96 15*9f fe 15*9f 9e 16*9f 9d 15*9f 9d 15*9f 9d 15*9f 9c 15*9f 9b 15*9f 9b 15*9f 9b 15*9f 9b
  //   15*9f 9d 15*9f 9e 9d 14*9f 9e 9d 14*9f 9e 9d 14*9f 9e 9c 14*9f 9e 9b 14*9f 9e 9b 14*9f 9e 9b 14*9f
  //   9e 9b 14*9f 9e 9d 15*9f 9d 15*9f 9d 15*9f 9d 15*9f 9c 15*9f 9b 15*9f 9b 15*9f 9b 15*9f 9b 15*9f 9d
  //   14*9f 9b 9f 9d 12*9f 9d bf 14*9f 9d bf 14*9f 9d bf 14*9f 9c bf 15*9f 9b 9d bf 13*9f 9e 9b 9d bf
  //   13*9f 9b 9d bf 11*9f 9d bf 14*9f db 15*9f db 15*9f db 15*9f db 16*9f db 9d 13*9f db 9f 9e 9d 12*9f
  //   db 9f 9f 9d 333*9f 9b 9d 14*9f 9b 9d 14*9f 9b 9d 14*9f 9b 9d 334*9f 9b 9d 14*9f 9b 9d 14*9f 9b 9d
  //   14*9f 9b 9d 334*9f 9b 15*9f 9b 15*9f 9b 15*9f 9b 335*9f 9b 9d 14*9f 9b 9d 14*9f 9b 9d 14*9f 9b 9d
  //   334*9f 9b 9d 14*9f 9b 9d 14*9f 9b 9d 14*9f 9b 9d 334*9f 9b 9d 14*9f 9b 9d 14*9f 9b 9d 14*9f 9b 9d
  //   78*9f 9b 9d 78*9f 9b 9d 78*9f 9b 9d 78*9f 9e 31*9f 9e 15*9f 9e 143*9f 9e 16*9f 9d bd bf 12*9f 9e 9d
  //   bd bf 11*9f db db 14*9f db db db 4173*9f
  //   contents of EEPROM2 (hex, n*v repeats v):
  //   32*f e d 14*f e d 414*f d 15*f d 15*f d 15*f d 15*f d 15*f d 15*f d 15*f d 15*f d 15*f e d 14*f e d
  //   14*f e d 14*f e d 14*f e d 14*f e d 14*f e d 14*f e d 14*f e d 14*f e d 14*f e d 14*f e d 14*f e d
  //   14*f e d 14*f e d 14*f e d 14*f e d 14*f e d 14*f d b d 7 76*f d b 7 13*f e d b 7 12*f e d b 7 92*f
  //   d b 7 13*f b e d 7 12*f b e d 7 28*f 8f 31*f 8f 15*f 1f 15*f 9f 15*f 1f 15*f 9f 15*f 2f 15*f af 15*f
  //   2f 15*f af 15*f 3f 15*f bf 15*f 3f 15*f bf 15*f b 15*f b 1f 14*f b 2f 14*f b 3f 14*f d b 4f 13*f d b
  //   cf 13*f d b 4f 13*f d b cf 29*f 8f 31*f 8f 15*f 1f 15*f 9f 15*f 1f 15*f 9f 15*f 2f 15*f af 15*f 2f
  //   15*f af 15*f 3f 15*f bf 15*f 3f 15*f bf 15*f b 15*f b 1f 14*f b 2f 14*f b 3f 14*f d b 4f 13*f d b cf
  //   13*f d b 4f 13*f d b cf 29*f 8f 31*f 8f 15*f 1f 15*f 9f 15*f 1f 15*f 9f 15*f 2f 15*f af 15*f 2f 15*f
  //   af 15*f 3f 15*f bf 15*f 3f 15*f bf 15*f b 15*f b 1f 14*f b 2f 14*f b 3f 14*f d b 4f 13*f d b cf 13*f
  //   d b 4f 13*f d b cf 29*f 8f 31*f 8f 15*f 1f 15*f 9f 15*f 1f 15*f 9f 15*f 2f 15*f af 15*f 2f 15*f af
  //   15*f 3f 15*f bf 15*f 3f 15*f bf 15*f b 15*f b 1f 14*f b 2f 14*f b 3f 14*f d b 4f 13*f d b cf 13*f d
  //   b 4f 13*f d b cf 29*f 8f 31*f 8f 15*f 1f 15*f 9f 15*f 1f 15*f 9f 15*f 2f 15*f af 15*f 2f 15*f af
  //   15*f 3f 15*f bf 15*f 3f 15*f bf 15*f b 15*f b 1f 14*f b 2f 14*f b 3f 14*f d b 4f 13*f d b cf 13*f d
  //   b 4f 13*f d b cf 29*f 8f 31*f 8f 15*f 1f 15*f 9f 15*f 1f 15*f 9f 15*f 2f 15*f af 15*f 2f 15*f af
  //   15*f 3f 15*f bf 15*f 3f 15*f bf 15*f b 15*f b 1f 14*f b 2f 14*f b 3f 14*f d b 4f 13*f d b cf 13*f d
  //   b 4f 13*f d b cf 29*f 1f 15*f 2f 15*f 3f 15*f d b 4f 13*f 8f 15*f 9f 15*f af 15*f bf 15*f d b cf
  //   13*f 8f 15*f 9f 15*f af 15*f bf 15*f d b cf 45*f b f 7 13*f b f 7 13*f b f 7 13*f b f 7 13*f b f 7
  //   13*f b f 7 13*f d 15*f d 15*f d 15*f d 15*f e d 14*f e d 14*f e d 14*f e d 14*f e d 14*f e d 14*f e
  //   d 14*f d e 15*f d e 4173*f
  //   contents of EEPROM3 (hex, n*v repeats v):
  //   60 15*e0 60 15*e0 60 4*e0 80 60 14*e0 80 60 9*e0 60 60 14*e0 60 60 14*e0 60 60 14*e0 60 60 14*e0 60
  //   60 14*e0 60 60 14*e0 60 60 14*e0 60 15*e0 60 15*e0 60 15*e0 60 15*e0 60 15*e0 60 15*e0 60 15*e0 60
  //   15*e0 60 15*e0 60 15*e0 60 15*e0 60 15*e0 60 15*e0 60 15*e0 60 15*e0 60 15*e0 60 15*e0 60 15*e0 60
  //   60 14*e0 60 60 14*e0 60 60 14*e0 60 60 14*e0 60 60 14*e0 60 60 14*e0 60 60 14*e0 60 60 14*e0 60 60
  //   60 15*e0 60 15*e0 60 15*e0 60 15*e0 60 15*e0 60 15*e0 60 15*e0 60 15*e0 60 15*e0 60 60 12*e0 60 60
  //   60 13*e0 60 60 60 13*e0 60 60 60 13*e0 60 60 60 13*e0 60 60 60 13*e0 60 60 60 13*e0 60 60 60 13*e0
  //   60 60 60 13*e0 4*60 12*e0 60 e0 60 60 13*e0 60 15*e0 60 15*e0 60 15*e0 60 14*e0 60 e0 e0 60 16*e0 60
  //   11*e0 60 60 e0 e0 60 11*e0 60 60 14*e0 60 15*e0 60 15*e0 60 15*e0 60 15*e0 60 e0 60 16*e0 60 13*e0
  //   60 60 60 12*e0 64 15*e0 64 15*e0 65 15*e0 65 15*e0 64 15*e0 64 15*e0 65 15*e0 65 15*e0 64 15*e0 64
  //   15*e0 65 15*e0 65 15*e0 64 15*e0 64 15*e0 65 15*e0 65 15*e0 60 66 14*e0 60 66 14*e0 60 66 14*e0 60
  //   66 14*e0 60 e0 64 13*e0 60 e0 64 13*e0 60 e0 65 13*e0 60 e0 65 13*e0 68 15*e0 68 15*e0 69 15*e0 69
  //   15*e0 68 15*e0 68 15*e0 69 15*e0 69 15*e0 68 15*e0 68 15*e0 69 15*e0 69 15*e0 68 15*e0 68 15*e0 69
  //   15*e0 69 15*e0 60 6a 14*e0 60 6a 14*e0 60 6a 14*e0 60 6a 14*e0 60 e0 68 13*e0 60 e0 68 13*e0 60 e0
  //   69 13*e0 60 e0 69 13*e0 68 15*e0 68 15*e0 69 15*e0 69 15*e0 68 15*e0 68 15*e0 69 15*e0 69 15*e0 68
  //   15*e0 68 15*e0 69 15*e0 69 15*e0 68 15*e0 68 15*e0 69 15*e0 69 15*e0 60 6a 14*e0 60 6a 14*e0 60 6a
  //   14*e0 60 6a 14*e0 60 e0 68 13*e0 60 e0 68 13*e0 60 e0 69 13*e0 60 e0 69 13*e0 6c 15*e0 6c 15*e0 6d
  //   15*e0 6d 15*e0 6c 15*e0 6c 15*e0 6d 15*e0 6d 15*e0 6c 15*e0 6c 15*e0 6d 15*e0 6d 15*e0 6c 15*e0 6c
  //   15*e0 6d 15*e0 6d 15*e0 60 6e 14*e0 60 6e 14*e0 60 6e 14*e0 60 6e 14*e0 60 e0 6c 13*e0 60 e0 6c
  //   13*e0 60 e0 6d 13*e0 60 e0 6d 13*e0 70 15*e0 70 15*e0 71 15*e0 71 15*e0 70 15*e0 70 15*e0 71 15*e0
  //   71 15*e0 70 15*e0 70 15*e0 71 15*e0 71 15*e0 70 15*e0 70 15*e0 71 15*e0 71 15*e0 60 72 14*e0 60 72
  //   14*e0 60 72 14*e0 60 72 14*e0 60 e0 70 13*e0 60 e0 70 13*e0 60 e0 71 13*e0 60 e0 71 13*e0 74 15*e0
  //   74 15*e0 75 15*e0 75 15*e0 74 15*e0 74 15*e0 75 15*e0 75 15*e0 74 15*e0 74 15*e0 75 15*e0 75 15*e0
  //   74 15*e0 74 15*e0 75 15*e0 75 15*e0 60 76 14*e0 60 76 14*e0 60 76 14*e0 60 76 14*e0 60 e0 74 13*e0
  //   60 e0 74 13*e0 60 e0 75 13*e0 60 e0 75 13*e0 78 15*e0 78 15*e0 78 15*e0 78 15*e0 60 e0 78 13*e0 66
  //   15*e0 66 15*e0 66 15*e0 66 15*e0 60 e0 66 13*e0 6a 15*e0 6a 15*e0 6a 15*e0 6a 15*e0 60 e0 6a 13*e0
  //   60 15*e0 60 17*e0 60 15*e0 60 15*e0 60 15*e0 60 15*e0 60 15*e0 60 13*e0 60 a0 60 13*e0 60 a0 60
  //   13*e0 60 a0 60 13*e0 60 a0 60 13*e0 60 60 80 60 12*e0 60 60 80 60 12*e0 60 60 80 60 12*e0 60 60 80
  //   60 14*e0 80 60 12*e0 60 60 e0 e0 80 60 14*e0 80 60 12*e0 80 60 15*e0 80 60 11*e0 60 15*e0 60 15*e0
  //   60 15*e0 60 4111*e0
  //   contents of EEPROM4 (hex, n*v repeats v):
  //   3 15*83 3 17*83 82 81 83 87 3 11*83 82 81 83 87 3 10*83 3 15*83 3 15*83 3 15*83 3 15*83 3 15*83 3
  //   15*83 3 14*83 3 15*83 3 15*83 3 15*83 3 15*83 3 15*83 3 15*83 3 15*83 3 15*83 3 15*83 3 15*83 3
  //   15*83 3 15*83 3 15*83 3 15*83 3 15*83 3 15*83 3 15*83 3 16*83 3 15*83 3 15*83 3 15*83 3 15*83 3
  //   15*83 3 15*83 3 15*83 3 16*83 3 15*83 3 15*83 3 15*83 3 15*83 3 15*83 3 15*83 3 15*83 3 15*83 3
  //   16*83 3 14*83 3 15*83 3 15*83 3 15*83 3 15*83 3 15*83 3 15*83 3 15*83 3 16*83 3 15*83 3 13*83 3
  //   15*83 3 15*83 3 15*83 3 17*83 3 16*83 3 15*83 3 12*83 3 14*83 3 15*83 3 15*83 3 15*83 3 17*83 3
  //   16*83 3 15*83 3 12*83 3 15*83 3 15*83 3 15*83 3 15*83 3 15*83 3 15*83 3 15*83 3 15*83 3 15*83 3
  //   15*83 3 15*83 3 15*83 3 15*83 3 15*83 3 15*83 3 16*83 3 15*83 3 15*83 3 15*83 3 16*83 3 15*83 3
  //   15*83 3 15*83 3 13*83 3 15*83 3 15*83 3 15*83 3 15*83 3 15*83 3 15*83 3 15*83 3 15*83 3 15*83 3
  //   15*83 3 15*83 3 15*83 3 15*83 3 15*83 3 15*83 3 16*83 3 15*83 3 15*83 3 15*83 3 16*83 3 15*83 3
  //   15*83 3 15*83 3 13*83 3 15*83 3 15*83 3 15*83 3 15*83 3 15*83 3 15*83 3 15*83 3 15*83 3 15*83 3
  //   15*83 3 15*83 3 15*83 3 15*83 3 15*83 3 15*83 3 16*83 3 15*83 3 15*83 3 15*83 3 16*83 3 15*83 3
  //   15*83 3 15*83 3 13*83 3 15*83 3 15*83 3 15*83 3 15*83 3 15*83 3 15*83 3 15*83 3 15*83 3 15*83 3
  //   15*83 3 15*83 3 15*83 3 15*83 3 15*83 3 15*83 3 16*83 3 15*83 3 15*83 3 15*83 3 16*83 3 15*83 3
  //   15*83 3 15*83 3 13*83 3 15*83 3 15*83 3 15*83 3 15*83 3 15*83 3 15*83 3 15*83 3 15*83 3 15*83 3
  //   15*83 3 15*83 3 15*83 3 15*83 3 15*83 3 15*83 3 16*83 3 15*83 3 15*83 3 15*83 3 16*83 3 15*83 3
  //   15*83 3 15*83 3 13*83 3 15*83 3 15*83 3 15*83 3 15*83 3 15*83 3 15*83 3 15*83 3 15*83 3 15*83 3
  //   15*83 3 15*83 3 15*83 3 15*83 3 15*83 3 15*83 3 16*83 3 15*83 3 15*83 3 15*83 3 16*83 3 15*83 3
  //   15*83 3 15*83 3 13*83 3 15*83 3 15*83 3 15*83 3 17*83 3 13*83 3 15*83 3 15*83 3 15*83 3 17*83 3
  //   13*83 3 15*83 3 15*83 3 15*83 3 17*83 3 13*83 3 15*83 3 17*83 3 15*83 3 15*83 3 15*83 3 15*83 3
  //   15*83 3 14*83 8b 3 14*83 a3 3 14*83 93 3 14*83 87 3 15*83 8b 3 14*83 a3 3 14*83 93 3 14*83 87 3
  //   14*83 87 3 14*83 82 81 87 3 12*83 82 81 87 3 12*83 87 3 15*83 87 3 11*83 3 15*83 3 15*83 3 15*83 3
  //   4111*83
  //   contents of EEPROM5 (hex, n*v repeats v):
  //   71 15*79 70 15*79 59 39 7d 7d 7d f9 71 9*79 59 39 7d 7d 7d f9 71 9*79 61 71 14*79 61 71 14*79 61 71
  //   14*79 61 71 14*79 61 71 14*79 61 71 14*79 61 71 14*79 71 15*79 71 15*79 71 15*79 71 15*79 71 15*79
  //   71 15*79 71 15*79 71 15*79 71 15*79 71 15*79 71 15*79 71 15*79 71 15*79 71 15*79 71 15*79 71 15*79
  //   71 15*79 71 15*79 61 73 14*79 61 73 14*79 61 73 14*79 61 73 14*79 61 73 14*79 61 73 14*79 61 73
  //   14*79 61 73 14*79 61 63 71 15*79 71 15*79 71 15*79 71 15*79 71 15*79 71 15*79 71 15*79 71 15*79 71
  //   15*79 61 71 12*79 61 61 71 13*79 61 61 71 13*79 61 61 71 13*79 61 61 71 13*79 61 61 71 13*79 61 61
  //   71 13*79 61 61 71 13*79 61 61 71 13*79 61 61 61 71 12*79 61 7b 61 73 12*79 7d 71 14*79 7d 71 14*79
  //   7d 71 14*79 7d 71 14*79 61 7b 7d 71 15*79 7d 71 11*79 61 61 79 7d 71 11*79 65 71 14*79 75 15*79 75
  //   15*79 75 15*79 75 15*79 61 7d 73 13*79 7d 79 79 71 12*79 7d 61 61 71 12*79 f1 15*79 f1 15*79 f1
  //   15*79 f1 15*79 f1 15*79 f1 15*79 f1 15*79 f1 15*79 f1 15*79 f1 15*79 f1 15*79 f1 15*79 f1 15*79 f1
  //   15*79 f1 15*79 f1 15*79 61 f1 14*79 61 f1 14*79 61 f1 14*79 61 f1 14*79 61 7b f3 13*79 61 7b f3
  //   13*79 61 7b f3 13*79 61 7b f3 13*79 f1 15*79 f1 15*79 f1 15*79 f1 15*79 f1 15*79 f1 15*79 f1 15*79
  //   f1 15*79 f1 15*79 f1 15*79 f1 15*79 f1 15*79 f1 15*79 f1 15*79 f1 15*79 f1 15*79 61 f1 14*79 61 f1
  //   14*79 61 f1 14*79 61 f1 14*79 61 7b f3 13*79 61 7b f3 13*79 61 7b f3 13*79 61 7b f3 13*79 f1 15*79
  //   f1 15*79 f1 15*79 f1 15*79 f1 15*79 f1 15*79 f1 15*79 f1 15*79 f1 15*79 f1 15*79 f1 15*79 f1 15*79
  //   f1 15*79 f1 15*79 f1 15*79 f1 15*79 61 f1 14*79 61 f1 14*79 61 f1 14*79 61 f1 14*79 61 7b f1 13*79
  //   61 7b f1 13*79 61 7b f1 13*79 61 7b f1 13*79 f1 15*79 f1 15*79 f1 15*79 f1 15*79 f1 15*79 f1 15*79
  //   f1 15*79 f1 15*79 f1 15*79 f1 15*79 f1 15*79 f1 15*79 f1 15*79 f1 15*79 f1 15*79 f1 15*79 61 f1
  //   14*79 61 f1 14*79 61 f1 14*79 61 f1 14*79 61 7b f3 13*79 61 7b f3 13*79 61 7b f3 13*79 61 7b f3
  //   13*79 f1 15*79 f1 15*79 f1 15*79 f1 15*79 f1 15*79 f1 15*79 f1 15*79 f1 15*79 f1 15*79 f1 15*79 f1
  //   15*79 f1 15*79 f1 15*79 f1 15*79 f1 15*79 f1 15*79 61 f1 14*79 61 f1 14*79 61 f1 14*79 61 f1 14*79
  //   61 7b f3 13*79 61 7b f3 13*79 61 7b f3 13*79 61 7b f3 13*79 f1 15*79 f1 15*79 f1 15*79 f1 15*79 f1
  //   15*79 f1 15*79 f1 15*79 f1 15*79 f1 15*79 f1 15*79 f1 15*79 f1 15*79 f1 15*79 f1 15*79 f1 15*79 f1
  //   15*79 61 f1 14*79 61 f1 14*79 61 f1 14*79 61 f1 14*79 61 7b f3 13*79 61 7b f3 13*79 61 7b f3 13*79
  //   61 7b f3 13*79 f1 15*79 f1 15*79 f1 15*79 f1 15*79 61 7b f3 13*79 f1 15*79 f1 15*79 f1 15*79 f1
  //   15*79 61 7b f3 13*79 f1 15*79 f1 15*79 f1 15*79 f1 15*79 61 7b f3 13*79 71 15*79 71 17*79 71 15*79
  //   71 15*79 71 15*79 71 15*79 71 15*79 71 13*79 61 79 71 13*79 61 79 71 13*79 61 79 71 13*79 61 79 71
  //   13*79 61 61 79 71 12*79 61 61 79 71 12*79 61 61 79 71 12*79 61 61 79 71 15*79 71 12*79 61 61 7d 7d
  //   79 71 12*79 7d 7d 79 71 10*79 7d 7d 79 71 12*79 7d 7d 7d 79 71 11*79 71 15*79 f1 15*79 71 15*79 f1
  //   4111*79
  //   contents of EEPROM6 (hex, n*v repeats v):
  //   32*3c 34 3c 3c 3c 38 3e 14*3c 38 3e 106*3c 2c 47*3c 1c 239*3c 2c 703*3c 3d 15*3c 3d 15*3c 3d 15*3c
  //   3d 15*3c 3d 15*3c 3d 15*3c 3d 15*3c 3d 15*3c 3d 15*3c 3d 15*3c 3d 15*3c 3d 15*3c 3d 15*3c 3d 15*3c
  //   3d 15*3c 3d 16*3c 3d 15*3c 3d 15*3c 3d 15*3c 3d 16*3c 3d 15*3c 3d 15*3c 3d 15*3c 3d 13*3c 3d 15*3c
  //   3d 15*3c 3d 15*3c 3d 15*3c 3d 15*3c 3d 15*3c 3d 15*3c 3d 15*3c 3d 15*3c 3d 15*3c 3d 15*3c 3d 15*3c
  //   3d 15*3c 3d 15*3c 3d 15*3c 3d 16*3c 3d 15*3c 3d 15*3c 3d 15*3c 3d 16*3c 3d 15*3c 3d 15*3c 3d 15*3c
  //   3d 13*3c 3d 15*3c 3d 15*3c 3d 15*3c 3d 15*3c 3d 15*3c 3d 15*3c 3d 15*3c 3d 15*3c 3d 15*3c 3d 15*3c
  //   3d 15*3c 3d 15*3c 3d 15*3c 3d 15*3c 3d 15*3c 3d 16*3c 3d 15*3c 3d 15*3c 3d 15*3c 3d 16*3c 3d 15*3c
  //   3d 15*3c 3d 15*3c 3d 13*3c 3d 15*3c 3d 15*3c 3d 15*3c 3d 15*3c 3d 15*3c 3d 15*3c 3d 15*3c 3d 15*3c
  //   3d 15*3c 3d 15*3c 3d 15*3c 3d 15*3c 3d 15*3c 3d 15*3c 3d 15*3c 3d 16*3c 3d 15*3c 3d 15*3c 3d 15*3c
  //   3d 16*3c 3d 15*3c 3d 15*3c 3d 15*3c 3d 13*3c 3d 15*3c 3d 15*3c 3d 15*3c 3d 15*3c 3d 15*3c 3d 15*3c
  //   3d 15*3c 3d 15*3c 3d 15*3c 3d 15*3c 3d 15*3c 3d 15*3c 3d 15*3c 3d 15*3c 3d 15*3c 3d 16*3c 3d 15*3c
  //   3d 15*3c 3d 15*3c 3d 16*3c 3d 15*3c 3d 15*3c 3d 15*3c 3d 13*3c 3d 15*3c 3d 15*3c 3d 15*3c 3d 15*3c
  //   3d 15*3c 3d 15*3c 3d 15*3c 3d 15*3c 3d 15*3c 3d 15*3c 3d 15*3c 3d 15*3c 3d 15*3c 3d 15*3c 3d 15*3c
  //   3d 16*3c 3d 15*3c 3d 15*3c 3d 15*3c 3d 16*3c 3d 15*3c 3d 15*3c 3d 15*3c 3d 13*3c 3d 15*3c 3d 15*3c
  //   3d 15*3c 3d 17*3c 3d 13*3c 3d 15*3c 3d 15*3c 3d 15*3c 3d 17*3c 3d 13*3c 3d 15*3c 3d 15*3c 3d 15*3c
  //   3d 17*3c 3d 333*3c 3d 15*3c 3e 15*3c 3e 15*3c 3f 15*3c 3f 4111*3c
endmodule

module AddrDecoder (
  input  [15:0] ABUS,
  output NOT_DEVICE_SEL_ROM,
  output NOT_DEVICE_SEL_RAM,
  output NOT_DEVICE_SEL_0,
  output NOT_DEVICE_SEL_1,
  output NOT_DEVICE_SEL_2,
  output NOT_DEVICE_SEL_3,
  output NOT_DEVICE_SEL_4,
  output NOT_DEVICE_SEL_5
);

  wire decoder_1_out0, decoder_1_out1, decoder_1_out2, decoder_1_out3, decoder_1_out4, decoder_1_out5,
       decoder_1_out6, decoder_1_out7;

  Decoder #(.select(3)) decoder_1 (
    .out0(decoder_1_out0), .out1(decoder_1_out1), .out2(decoder_1_out2), .out3(decoder_1_out3),
    .out4(decoder_1_out4), .out5(decoder_1_out5), .out6(decoder_1_out6), .out7(decoder_1_out7),
    .sel(ABUS[15:13]), .en(1'b1));
  not not_1 (NOT_DEVICE_SEL_ROM, decoder_1_out0);
  not not_2 (NOT_DEVICE_SEL_RAM, decoder_1_out1);
  not not_3 (NOT_DEVICE_SEL_0, decoder_1_out2);
  not not_4 (NOT_DEVICE_SEL_1, decoder_1_out3);
  not not_5 (NOT_DEVICE_SEL_2, decoder_1_out4);
  not not_6 (NOT_DEVICE_SEL_3, decoder_1_out5);
  not not_7 (NOT_DEVICE_SEL_4, decoder_1_out6);
  not not_8 (NOT_DEVICE_SEL_5, decoder_1_out7);
endmodule

module AddressSelector (
  input  [7:0] ABL_in,
  input  [7:0] ABH_in,
  input  [7:0] DS_IN,
  input  [15:0] SS_SP_in,
  input  [15:0] CS_PC_in,
  input  ADDR_SEL0,
  input  ADDR_SEL1,
  input  CSPC_override,
  output [15:0] ADDR_OUT
);

  wire [1:0] or_1_out;

  or or_1 (or_1_out[0], ADDR_SEL0, CSPC_override);
  or or_2 (or_1_out[1], ADDR_SEL1, CSPC_override);
  Multiplexer #(.select(2), .width(16)) multiplexer_1 (
    .in0({ABH_in, ABL_in}), .in1({DS_IN, ABL_in}), .in2(SS_SP_in), .in3(CS_PC_in), .out(ADDR_OUT),
    .sel(or_1_out));

  // Notes on the sheet:
  //   01: DS:ABL
  //   10: SS:SP
  //   11: CS:PC
  //   00: ABH:ABL
endmodule

module FLAGSController (
  input  MODE2,
  input  MODE1,
  input  MODE0,
  input  [3:0] BUS_IN,
  input  [2:0] ALU_IN,
  output NOT_C_IN,
  output NOT_Z_IN,
  output NOT_N_IN,
  output NOT_I_IN,
  output C_VAL,
  output Z_VAL,
  output N_VAL,
  output I_VAL
);

  wire and_1_out, not_1_out, not_3_out, or_3_out, or_4_out, or_5_out, or_6_out, or_7_out, or_8_out, or_9_out,
       or_10_out, or_11_out, or_12_out, or_13_out, or_14_out, or_15_out;

  not not_1 (not_1_out, MODE2);
  not not_2 (NOT_C_IN, MODE1);
  not not_3 (not_3_out, MODE0);
  or or_1 (NOT_Z_IN, MODE2, NOT_C_IN);
  or or_2 (NOT_N_IN, MODE2, NOT_C_IN);
  or or_3 (or_3_out, not_1_out, MODE1);
  or or_4 (or_4_out, MODE2, NOT_C_IN);
  or or_5 (or_5_out, or_4_out, MODE0);
  or or_6 (or_6_out, MODE0, BUS_IN[0]);
  and and_1 (and_1_out, or_6_out, or_7_out);
  or or_7 (or_7_out, not_1_out, MODE0);
  or or_8 (or_8_out, MODE2, not_3_out);
  or or_9 (or_9_out, or_8_out, ALU_IN[0]);
  or or_10 (or_10_out, MODE0, BUS_IN[1]);
  and and_2 (Z_VAL, or_10_out, or_11_out);
  or or_11 (or_11_out, not_3_out, ALU_IN[1]);
  or or_12 (or_12_out, MODE0, BUS_IN[2]);
  and and_3 (N_VAL, or_12_out, or_13_out);
  or or_13 (or_13_out, not_3_out, ALU_IN[2]);
  or or_14 (or_14_out, MODE0, BUS_IN[3]);
  and and_4 (I_VAL, or_14_out, or_15_out);
  or or_15 (or_15_out, MODE1, MODE0);
  and and_5 (NOT_I_IN, or_3_out, or_5_out);
  and and_6 (C_VAL, and_1_out, or_9_out);
endmodule

module TwoPhaseClock (
  input  NOT_HLT,
  output BASE_CLK,
  output PHI1,
  output PHI2,
  output C1,
  output C2,
  output C3,
  output C4
);

  wire and_1_out, j_k_ff_1_q, j_k_ff_2_q, nor_1_out, nor_2_out, not_1_out, not_2_out, not_3_out, not_4_out,
       not_6_out;

  Clock clock_1 (.out(BASE_CLK));
  and and_1 (and_1_out, BASE_CLK, NOT_HLT);
  J_K_Flip_Flop j_k_ff_1 (.J(1'b1), .K(1'b1), .clk(and_1_out), .Q(j_k_ff_1_q));  // open: Qn, preset, reset
  not not_1 (not_1_out, j_k_ff_1_q);
  not not_2 (not_2_out, and_1_out);
  J_K_Flip_Flop j_k_ff_2 (.J(not_1_out), .K(not_1_out), .clk(not_2_out), .Q(j_k_ff_2_q));  // open: Qn, preset, reset
  not not_3 (not_3_out, j_k_ff_2_q);
  and and_2 (C1, j_k_ff_1_q, PHI1);
  and and_3 (C3, j_k_ff_1_q, PHI2);
  nor nor_1 (nor_1_out, not_3_out, PHI2);
  not not_4 (not_4_out, nor_1_out);
  not not_5 (PHI1, not_4_out);
  nor nor_2 (nor_2_out, PHI1, j_k_ff_2_q);
  not not_6 (not_6_out, nor_2_out);
  not not_7 (PHI2, not_6_out);
  not not_8 (C2, C1);
  not not_9 (C4, C3);
endmodule

module DeviceOutputController (
  input  NOT_DEVICE_SEL,
  output NOT_DEVICE_OE
);

  wire undriven;

  or or_1 (NOT_DEVICE_OE, undriven, NOT_DEVICE_SEL);
endmodule

module DeviceOEPhaseSelector (
  input  NOT_DEVICE_OUT,
  input  NOT_FETCH,
  input  PHI1,
  input  PHI2,
  output NOT_DEVICE_OE
);

  wire or_1_out, or_2_out;

  or or_1 (or_1_out, NOT_DEVICE_OUT, PHI1);
  and and_1 (NOT_DEVICE_OE, or_1_out, or_2_out);
  or or_2 (or_2_out, NOT_FETCH, PHI2);
endmodule

module ResetCircuit (
  input  RESET_BTN,
  input  PHASE,
  output RESET_OUT
);

  D_Flip_Flop d_ff_1 (.D(1'b0), .clk(PHASE), .Q(RESET_OUT), .preset(RESET_BTN));  // open: Qn, reset
endmodule
