// Logisim project Devices.circ as structural Verilog: 6 circuits, main circuit ButtonAdapter
module ButtonAdapter (
  input  BUTTON_IN,
  input  [7:0] DBUS_IN,
  input  [15:0] ABUS,
  input  NOT_DEVICE_IN,
  input  NOT_DEVICE_OE,
  input  NOT_DEVICE_SEL,
  input  CLK,
  output NOT_IRQ,
  output [7:0] D_BUS_OUT
);

  wire nor_1_out, s_r_ff_1_q;

  nor nor_1 (nor_1_out, NOT_DEVICE_IN, NOT_DEVICE_SEL);
  S_R_Flip_Flop s_r_ff_1 (.S(BUTTON_IN), .R(nor_1_out), .clk(CLK), .Q(s_r_ff_1_q));  // open: reset, Qn, preset
  assign NOT_IRQ = s_r_ff_1_q ? 1'b0 : 1'bz;  // Controlled_Buffer controlled_buffer_1
  assign D_BUS_OUT = {{7{1'b0}}, s_r_ff_1_q};  // Bit_Extender bit_extender_1
endmodule

module HexDisplayAdapter (
  input  [7:0] DBUS_IN,
  input  [15:0] ABUS,
  input  NOT_DEVICE_IN,
  input  NOT_DEVICE_OE,
  input  NOT_DEVICE_SEL,
  input  CLK,
  output [3:0] LSB,
  output [3:0] MSB
);

  wire nor_1_out;

  nor nor_1 (nor_1_out, NOT_DEVICE_IN, NOT_DEVICE_SEL);
  Register register_1 (.D(DBUS_IN), .en(nor_1_out), .clk(CLK), .Q({MSB, LSB}));  // open: clr
endmodule

module KeyboardAdapter (
  input  K_AVAIL,
  input  [6:0] K_DATA,
  input  [7:0] BUS_IN,
  input  [15:0] ABUS,
  input  NOT_DEVICE_IN,
  input  NOT_DEVICE_OE,
  input  NOT_DEVICE_SEL,
  input  CLK,
  output NOT_IRQ,
  output [7:0] ASYNC_OUT,
  output K_READ_EN,
  output K_CLEAR,
  output K_CLK
);

  wire bit_extender_3_out, nor_2_out;
  wire [7:0] bit_extender_1_out, bit_extender_2_out;

  assign bit_extender_1_out = {{1{1'b0}}, K_DATA};  // Bit_Extender bit_extender_1
  and and_1 (K_READ_EN, nor_2_out, bit_extender_3_out);
  nor nor_1 (K_CLEAR, NOT_DEVICE_IN, NOT_DEVICE_SEL);
  nor nor_2 (nor_2_out, NOT_DEVICE_OE, NOT_DEVICE_SEL);
  assign bit_extender_2_out = {{7{1'b0}}, K_AVAIL};  // Bit_Extender bit_extender_2
  Transistor #(.\type ("n")) transistor_1 (.in(1'b0), .out(NOT_IRQ), .gate(K_AVAIL));
  Bit_Extender #(.in_width(16), .out_width(1)) bit_extender_3 (.in(ABUS), .out(bit_extender_3_out));
  Multiplexer #(.width(8)) multiplexer_1 (
    .in0(bit_extender_2_out), .in1(bit_extender_1_out), .out(ASYNC_OUT), .sel(bit_extender_3_out));

  assign K_CLK = CLK;
endmodule

module TTYAdapter (
  input  [7:0] DBUS_IN,
  input  [15:0] ABUS,
  input  NOT_DEVICE_IN,
  input  NOT_DEVICE_OE,
  input  NOT_DEVICE_SEL,
  input  CLK,
  output [6:0] TTY_DATA,
  output TTY_WE,
  output TTY_CLR
);

  wire bit_extender_1_out, nor_1_out, not_1_out;

  Bit_Extender #(.in_width(16), .out_width(1)) bit_extender_1 (.in(ABUS), .out(bit_extender_1_out));
  nor nor_1 (nor_1_out, NOT_DEVICE_IN, NOT_DEVICE_SEL);
  Bit_Extender #(.out_width(7)) bit_extender_2 (.in(DBUS_IN), .out(TTY_DATA));
  and and_1 (TTY_WE, nor_1_out, not_1_out);
  not not_1 (not_1_out, bit_extender_1_out);
  and and_2 (TTY_CLR, bit_extender_1_out, CLK, nor_1_out);
endmodule

module RGBScreenAdapter (
  input  [7:0] DBUS_IN,
  input  [15:0] ABUS,
  input  NOT_DEVICE_IN,
  input  NOT_DEVICE_OE,
  input  NOT_DEVICE_SEL,
  input  CLK,
  output DEVICE_RESET,
  output DEVICE_CLK,
  output DEVICE_WE,
  output [5:0] DEVICE_X,
  output [4:0] DEVICE_Y,
  output [7:0] DEVICE_DATA
);

  wire and_2_out;
  wire [12:0] bit_extender_1_out;

  nor nor_1 (DEVICE_WE, NOT_DEVICE_SEL, NOT_DEVICE_IN);
  and and_1 (DEVICE_RESET, DEVICE_WE, and_2_out);
  and and_2 (and_2_out, DBUS_IN[7], DBUS_IN[6], DBUS_IN[5], DBUS_IN[4], DBUS_IN[3], DBUS_IN[2], DBUS_IN[1], DBUS_IN[0], bit_extender_1_out[12], bit_extender_1_out[11], bit_extender_1_out[10], bit_extender_1_out[9], bit_extender_1_out[8], bit_extender_1_out[7], bit_extender_1_out[6], bit_extender_1_out[5], bit_extender_1_out[4], bit_extender_1_out[3], bit_extender_1_out[2], bit_extender_1_out[1], bit_extender_1_out[0]);
  Bit_Extender #(.in_width(16), .out_width(13)) bit_extender_1 (.in(ABUS), .out(bit_extender_1_out));

  assign DEVICE_CLK = CLK;
  assign DEVICE_DATA = DBUS_IN;
  assign DEVICE_X = ABUS[5:0];
  assign DEVICE_Y = ABUS[12:8];
endmodule

module JoystickAdapter (
  input  [7:0] DBUS_IN,
  input  [15:0] ABUS,
  input  NOT_DEVICE_IN,
  input  NOT_DEVICE_OE,
  input  NOT_DEVICE_SEL,
  input  CLK,
  input  [3:0] JX_IN,
  input  [3:0] JY_IN,
  output [7:0] ASYNC_OUT
);


  assign ASYNC_OUT = {JY_IN, JX_IN};
endmodule
